// Logisim project Lab1.circ as structural Verilog
module \一位二进制半加器  (
  input  A,
  input  B,
  output C,
  output S
);

  and and_1 (C, B, A);
  xor xor_1 (S, B, A);
endmodule

module \一位二进制全加器  (
  input  Ci,
  input  A,
  input  B,
  output C,
  output S
);

  wire and_1_out, and_2_out, and_3_out;

  and and_1 (and_1_out, A, Ci);
  and and_2 (and_2_out, B, Ci);
  and and_3 (and_3_out, B, A);
  xor xor_1 (S, Ci, A, B);
  or or_1 (C, and_1_out, and_2_out, and_3_out);
endmodule

module \串行进位并行加法器  (
  input  B3,
  input  B2,
  input  B1,
  input  B0,
  input  C0,
  input  A3,
  input  A2,
  input  A1,
  input  A0,
  output C,
  output S3,
  output S2,
  output S1,
  output S0
);

  wire \一位二进制全加器_1_c , \一位二进制全加器_2_c , \一位二进制全加器_3_c ;

  \一位二进制全加器  \u_一位二进制全加器_1  (.Ci(C0), .A(A0), .B(B0), .C(\一位二进制全加器_1_c ), .S(S0));
  \一位二进制全加器  \u_一位二进制全加器_2  (.Ci(\一位二进制全加器_1_c ), .A(A1), .B(B1), .C(\一位二进制全加器_2_c ), .S(S1));
  \一位二进制全加器  \u_一位二进制全加器_3  (.Ci(\一位二进制全加器_2_c ), .A(A2), .B(B2), .C(\一位二进制全加器_3_c ), .S(S2));
  \一位二进制全加器  \u_一位二进制全加器_4  (.Ci(\一位二进制全加器_3_c ), .A(A3), .B(B3), .C(C), .S(S3));
endmodule

module \先行进位并行加法器  (
  input  A3,
  input  B3,
  input  A2,
  input  B2,
  input  A1,
  input  B1,
  input  A0,
  input  B0,
  input  C0,
  output C4,
  output S3,
  output S2,
  output S1,
  output S0
);

  wire and_1_out, and_2_out, and_3_out, and_4_out, and_5_out, and_6_out, and_7_out, and_8_out, and_9_out,
       and_10_out, G0_out, G1_out, G2_out, G3_out, or_2_out, or_3_out, or_4_out, P0_out, P1_out, P2_out,
       P3_out;

  xor P3 (P3_out, A3, B3);
  and G3 (G3_out, A3, B3);
  xor P2 (P2_out, A2, B2);
  and G2 (G2_out, A2, B2);
  xor P1 (P1_out, A1, B1);
  and G1 (G1_out, A1, B1);
  xor P0 (P0_out, A0, B0);
  and G0 (G0_out, A0, B0);
  and and_1 (and_1_out, G0_out, P1_out, P2_out, P3_out);
  and and_2 (and_2_out, P0_out, C0, P3_out, P1_out, P2_out);
  and and_3 (and_3_out, P3_out, P2_out, G1_out);
  and and_4 (and_4_out, P3_out, G2_out);
  and and_5 (and_5_out, P1_out, P2_out, G0_out);
  and and_6 (and_6_out, P1_out, P2_out, P0_out, C0);
  and and_7 (and_7_out, P2_out, G1_out);
  and and_8 (and_8_out, P1_out, G0_out);
  and and_9 (and_9_out, P1_out, P0_out, C0);
  and and_10 (and_10_out, P0_out, C0);
  or or_1 (C4, and_1_out, and_2_out, G3_out, and_3_out, and_4_out);
  or or_2 (or_2_out, and_5_out, and_6_out, G2_out, and_7_out);
  or or_3 (or_3_out, and_9_out, and_8_out, G1_out);
  or or_4 (or_4_out, and_10_out, G0_out);
  xor xor_1 (S3, P3_out, or_2_out);
  xor xor_2 (S2, P2_out, or_3_out);
  xor xor_3 (S1, P1_out, or_4_out);
  xor xor_4 (S0, P0_out, C0);
endmodule

module \先行进位并行加法器测试电路  (
  input  C0,
  input  A3,
  input  A2,
  input  A1,
  input  A0,
  input  B3,
  input  B2,
  input  B1,
  input  B0,
  output S3,
  output S2,
  output S1,
  output S0,
  output C4
);

  \先行进位并行加法器  \u_先行进位并行加法器_1  (
    .A3(A3), .B3(B3), .A2(A2), .B2(B2), .A1(A1), .B1(B1), .A0(A0), .B0(B0), .C0(C0), .C4(C4), .S3(S3),
    .S2(S2), .S1(S1), .S0(S0));
endmodule

module test (
  input  A3,
  input  A2,
  input  A1,
  input  A0,
  input  B3,
  input  B2,
  input  B1,
  input  B0,
  output out_9,
  output out_10,
  output out_11,
  output out_12,
  output out_13,
  output out_14,
  output out_15,
  output out_16
);

  wire and_1_out, and_2_out, and_3_out, not_1_out, not_3_out, not_4_out, \先行进位并行加法器_2_c4 , \先行进位并行加法器_2_s0 ,
       \先行进位并行加法器_2_s1 , \先行进位并行加法器_2_s2 , \先行进位并行加法器_2_s3 ;

  and and_1 (and_1_out, \先行进位并行加法器_2_c4 , not_4_out, not_3_out);
  or or_1 (out_12, and_1_out, and_3_out, and_2_out);
  and and_2 (and_2_out, not_1_out, \先行进位并行加法器_2_s3 , \先行进位并行加法器_2_s2 );
  and and_3 (and_3_out, not_1_out, \先行进位并行加法器_2_s3 , \先行进位并行加法器_2_s1 );
  \先行进位并行加法器  \u_先行进位并行加法器_1  (
    .A3(1'b0), .B3(\先行进位并行加法器_2_s3 ), .A2(out_12), .B2(\先行进位并行加法器_2_s2 ), .A1(out_12), .B1(\先行进位并行加法器_2_s1 ),
    .A0(1'b0), .B0(\先行进位并行加法器_2_s0 ), .C0(1'b0), .S3(out_13), .S2(out_14), .S1(out_15), .S0(out_16));  // open: C4
  not not_1 (not_1_out, \先行进位并行加法器_2_c4 );
  // NOT_Gate not_2 has open pins: in=\先行进位并行加法器_2_s1 , out=open
  not not_3 (not_3_out, \先行进位并行加法器_2_s2 );
  not not_4 (not_4_out, \先行进位并行加法器_2_s3 );
  \先行进位并行加法器  \u_先行进位并行加法器_2  (
    .A3(A3), .B3(B3), .A2(A2), .B2(B2), .A1(A1), .B1(B1), .A0(A0), .B0(B0), .C0(1'b0), .C4(\先行进位并行加法器_2_c4 ),
    .S3(\先行进位并行加法器_2_s3 ), .S2(\先行进位并行加法器_2_s2 ), .S1(\先行进位并行加法器_2_s1 ), .S0(\先行进位并行加法器_2_s0 ));

  assign out_9 = 1'b0;
  assign out_10 = 1'b0;
  assign out_11 = 1'b0;
endmodule

module test2 (
  input  B3,
  input  B2,
  input  B1,
  input  B0,
  input  A3,
  input  A2,
  input  A1,
  input  A0,
  output C7,
  output C6,
  output C5,
  output C4,
  output C3,
  output C2,
  output C1,
  output C0
);

  wire and_1_out, and_2_out, xor_1_out, xor_2_out, \先行进位并行加法器_2_c4 ;

  \先行进位并行加法器  \u_先行进位并行加法器_1  (
    .A3(1'b0), .B3(1'b0), .A2(1'b0), .B2(B3), .A1(and_1_out), .B1(B2), .A0(xor_1_out), .B0(B1),
    .C0(\先行进位并行加法器_2_c4 ), .S3(C7), .S2(C6), .S1(C5), .S0(C4));  // open: C4
  and and_1 (and_1_out, and_2_out, B3);
  xor xor_1 (xor_1_out, and_2_out, B3);
  and and_2 (and_2_out, B2, B0);
  \先行进位并行加法器  \u_先行进位并行加法器_2  (
    .A3(xor_2_out), .B3(A3), .A2(B1), .B2(A2), .A1(B0), .B1(A1), .A0(1'b0), .B0(A0), .C0(1'b0),
    .C4(\先行进位并行加法器_2_c4 ), .S3(C3), .S2(C2), .S1(C1), .S0(C0));
  xor xor_2 (xor_2_out, B2, B0);
endmodule

module test3 (
  input  C,
  input  B,
  input  A,
  output F1,
  output F2,
  output F3
);

  wire decoder_1_out0, decoder_1_out1, decoder_1_out2, decoder_1_out3, decoder_1_out6, decoder_1_out7;

  Decoder #(.select(3), .enable("false")) decoder_1 (
    .out0(decoder_1_out0), .out1(decoder_1_out1), .out2(decoder_1_out2), .out3(decoder_1_out3),
    .out6(decoder_1_out6), .out7(decoder_1_out7), .sel({A, B, C}));  // open: out4, out5
  or or_1 (F1, decoder_1_out0, decoder_1_out6, decoder_1_out2);
  or or_2 (F2, decoder_1_out0, decoder_1_out2, decoder_1_out3, decoder_1_out1, decoder_1_out6, decoder_1_out7);
  or or_3 (F3, decoder_1_out0, decoder_1_out1, decoder_1_out6, decoder_1_out7);
endmodule
