// Logisim project Lab2.circ as structural Verilog: 10 circuits, main circuit 四位二进制可逆计数器
module \四位二进制可逆计数器  (
  input  D,
  input  C,
  input  B,
  input  A,
  input  nLD,
  input  CPu,
  input  CPd,
  input  CLR,
  output QD,
  output QC,
  output QB,
  output QA
);

  wire and_1_out, and_2_out, and_3_out, and_4_out, and_5_out, and_6_out, and_7_out, and_8_out, and_9_out,
       and_10_out, and_11_out, d_ff_1_qn, d_ff_2_qn, d_ff_3_qn, d_ff_4_qn, nor_1_out, nor_2_out, nor_3_out,
       not_1_out, not_2_out, not_3_out, not_4_out, not_5_out, not_6_out, or_1_out, or_2_out, or_3_out,
       or_4_out, or_5_out, or_6_out, or_7_out, or_8_out;

  not not_1 (not_1_out, CPd);
  not not_2 (not_2_out, nLD);
  and and_1 (and_1_out, CPu, QC, QA, QB);
  nor nor_1 (nor_1_out, not_1_out, QC, QA, QB);
  and and_2 (and_2_out, CPu, QA, QB);
  nor nor_2 (nor_2_out, not_1_out, QA, QB);
  and and_3 (and_3_out, CPu, QA);
  nor nor_3 (nor_3_out, not_1_out, QA);
  and and_4 (and_4_out, not_2_out, D);
  or or_1 (or_1_out, and_1_out, nor_1_out);
  or or_2 (or_2_out, and_2_out, nor_2_out);
  or or_3 (or_3_out, and_3_out, nor_3_out);
  or or_4 (or_4_out, CPu, CPd);
  not not_3 (not_3_out, D);
  and and_5 (and_5_out, not_3_out, not_2_out);
  D_Flip_Flop #(.trigger("falling"), .Pre_Clr_Positions("LEGACY"), .NegatePresetClear("false"), .enable("true"), .NewFFLayout("false")) d_ff_1 (
    .clk(or_1_out), .D(d_ff_1_qn), .Q(QD), .Qn(d_ff_1_qn), .preset(and_4_out), .reset(or_5_out));  // open: en
  or or_5 (or_5_out, CLR, and_5_out);
  and and_6 (and_6_out, not_2_out, C);
  D_Flip_Flop #(.trigger("falling"), .Pre_Clr_Positions("LEGACY"), .NegatePresetClear("false"), .enable("true"), .NewFFLayout("false")) d_ff_2 (
    .clk(or_2_out), .D(d_ff_2_qn), .Q(QC), .Qn(d_ff_2_qn), .preset(and_6_out), .reset(or_6_out));  // open: en
  or or_6 (or_6_out, CLR, and_8_out);
  not not_4 (not_4_out, C);
  and and_7 (and_7_out, not_2_out, B);
  and and_8 (and_8_out, not_4_out, not_2_out);
  not not_5 (not_5_out, B);
  and and_9 (and_9_out, not_5_out, not_2_out);
  D_Flip_Flop #(.trigger("falling"), .Pre_Clr_Positions("LEGACY"), .NegatePresetClear("false"), .enable("true"), .NewFFLayout("false")) d_ff_3 (
    .clk(or_3_out), .D(d_ff_3_qn), .Q(QB), .Qn(d_ff_3_qn), .preset(and_7_out), .reset(or_7_out));  // open: en
  or or_7 (or_7_out, CLR, and_9_out);
  and and_10 (and_10_out, not_2_out, A);
  or or_8 (or_8_out, CLR, and_11_out);
  not not_6 (not_6_out, A);
  and and_11 (and_11_out, not_6_out, not_2_out);
  D_Flip_Flop #(.trigger("falling"), .Pre_Clr_Positions("LEGACY"), .NegatePresetClear("false"), .enable("true"), .NewFFLayout("false")) d_ff_4 (
    .clk(or_4_out), .D(d_ff_4_qn), .Q(QA), .Qn(d_ff_4_qn), .preset(and_10_out), .reset(or_8_out));  // open: en
endmodule

module \四位二进制可逆计数器测试电路  (
  input  in_1,
  input  in_2,
  input  in_3,
  input  in_4,
  input  in_5,
  input  in_6,
  input  in_7,
  input  in_8,
  output out_9,
  output out_10,
  output out_11,
  output out_12
);

  \四位二进制可逆计数器  \u_四位二进制可逆计数器_1  (
    .nLD(in_8), .D(in_4), .C(in_5), .B(in_6), .A(in_7), .QD(out_9), .QC(out_10), .QB(out_11), .QA(out_12),
    .CLR(in_2), .CPu(in_1), .CPd(in_3));
endmodule

module \二进制转8421码电路  (
  input  in_1,
  input  in_2,
  input  in_3,
  input  in_4,
  output out_5,
  output out_6,
  output out_7,
  output out_8,
  output out_9,
  output out_10,
  output out_11,
  output out_12
);

  wire or_1_out;

  or or_1 (or_1_out, in_2, in_3);
  and Z (out_8, or_1_out, in_1);
  \先行进位并行加法器  \u_先行进位并行加法器_1  (
    .A3(in_1), .B3(1'b0), .A2(in_2), .B2(out_8), .A1(in_3), .B1(out_8), .A0(in_4), .B0(1'b0), .C0(1'b0),
    .S3(out_9), .S2(out_10), .S1(out_11), .S0(out_12));  // open: C4

  assign out_5 = 1'b0;
  assign out_6 = 1'b0;
  assign out_7 = 1'b0;
endmodule

module \二进制转8421码测试电路  (
  input  in_1,
  input  in_2,
  input  in_3,
  input  in_4,
  output out_5,
  output out_6,
  output out_7,
  output out_8,
  output out_9,
  output out_10,
  output out_11,
  output out_12
);

  \二进制转8421码电路  \u_二进制转8421码电路_1  (
    .out_5(out_5), .out_6(out_6), .out_7(out_7), .out_8(out_8), .out_9(out_9), .out_10(out_10),
    .out_11(out_11), .out_12(out_12), .in_1(in_1), .in_2(in_2), .in_3(in_3), .in_4(in_4));
endmodule

module \显示电路  (
  input  D,
  input  C,
  input  B,
  input  A,
  output a_2,
  output b_2,
  output c_2,
  output d_2,
  output e,
  output f,
  output g
);

  wire not_1_out, not_2_out, not_3_out, not_4_out, or_1_out, or_2_out, or_3_out, or_4_out, or_5_out,
       or_6_out, or_7_out, or_8_out, or_9_out, or_10_out, or_11_out, or_12_out, or_13_out, or_14_out,
       or_15_out, or_16_out, or_17_out;

  not not_1 (not_1_out, D);
  not not_2 (not_2_out, C);
  not not_3 (not_3_out, B);
  not not_4 (not_4_out, A);
  or or_1 (or_1_out, D, C, B, not_4_out);
  or or_2 (or_2_out, not_2_out, B, A);
  or or_3 (or_3_out, not_1_out, not_3_out);
  or or_4 (or_4_out, not_2_out, B, not_4_out);
  or or_5 (or_5_out, not_2_out, not_3_out, A);
  or or_6 (or_6_out, not_1_out, not_3_out);
  or or_7 (or_7_out, C, not_3_out, A);
  or or_8 (or_8_out, not_1_out, not_2_out);
  or or_9 (or_9_out, C, B, not_4_out);
  or or_10 (or_10_out, not_2_out, B, A);
  or or_11 (or_11_out, not_2_out, not_3_out, not_4_out);
  or or_12 (or_12_out, not_2_out, B);
  or or_13 (or_13_out, D, C, not_4_out);
  or or_14 (or_14_out, C, not_3_out);
  or or_15 (or_15_out, not_3_out, not_4_out);
  or or_16 (or_16_out, D, C, B);
  or or_17 (or_17_out, not_2_out, not_3_out, not_4_out);
  and and_1 (a_2, or_1_out, or_2_out, or_3_out);
  and and_2 (b_2, or_4_out, or_5_out, or_6_out);
  and and_3 (c_2, or_7_out, or_8_out);
  and and_4 (d_2, or_9_out, or_10_out, or_11_out);
  and and_5 (e, not_4_out, or_12_out);
  and and_6 (f, or_13_out, or_14_out, or_15_out);
  and and_7 (g, or_16_out, or_17_out);
endmodule

module \显示电路测试电路  (
  input  in_1,
  input  in_2,
  input  in_3,
  input  in_4
);

  wire \显示电路_1_a_2 , \显示电路_1_b_2 , \显示电路_1_c_2 , \显示电路_1_d_2 , \显示电路_1_e , \显示电路_1_f , \显示电路_1_g ;

  _7_Segment_Display #(.active("true")) u_7_segment_display_1 (
    .g(\显示电路_1_g ), .f(\显示电路_1_f ), .a(\显示电路_1_a_2 ), .b(\显示电路_1_b_2 ), .e(\显示电路_1_e ), .d(\显示电路_1_d_2 ),
    .c(\显示电路_1_c_2 ));  // open: dp
  \显示电路  \u_显示电路_1  (
    .D(in_1), .C(in_2), .a_2(\显示电路_1_a_2 ), .B(in_3), .A(in_4), .b_2(\显示电路_1_b_2 ), .c_2(\显示电路_1_c_2 ),
    .d_2(\显示电路_1_d_2 ), .e(\显示电路_1_e ), .f(\显示电路_1_f ), .g(\显示电路_1_g ));
endmodule

module \报警电路  (
  input  QD,
  input  QC,
  input  QB,
  input  QA,
  input  CPu,
  input  CPd,
  output ALARM,
  output INC,
  output DEC
);

  wire nand_1_out, not_1_out, or_1_out;

  or or_1 (or_1_out, QA, QB, QC, QD);
  not not_1 (not_1_out, nand_1_out);
  nand nand_1 (nand_1_out, QA, QB, QC, QD);
  and and_1 (ALARM, CPu, not_1_out);
  and and_2 (INC, CPu, nand_1_out);
  and and_3 (DEC, CPd, or_1_out);
endmodule

module \小型实验室门禁系统  (
  input  CPu,
  input  CPd,
  input  CLR,
  output out_4,
  output out_5,
  output out_6,
  output out_7,
  output out_8,
  output out_9,
  output out_10,
  output out_11,
  output out_12,
  output out_13,
  output out_14,
  output out_15,
  output out_16,
  output out_17,
  output ALARM
);

  wire \二进制转8421码电路_1_out_5 , \二进制转8421码电路_1_out_6 , \二进制转8421码电路_1_out_7 , \二进制转8421码电路_1_out_8 ,
       \二进制转8421码电路_1_out_9 , \二进制转8421码电路_1_out_10 , \二进制转8421码电路_1_out_11 , \二进制转8421码电路_1_out_12 ,
       \四位二进制可逆计数器_1_qa , \四位二进制可逆计数器_1_qb , \四位二进制可逆计数器_1_qc , \四位二进制可逆计数器_1_qd , \报警电路_1_dec , \报警电路_1_inc ;

  \报警电路  \u_报警电路_1  (
    .QD(\四位二进制可逆计数器_1_qd ), .QC(\四位二进制可逆计数器_1_qc ), .QB(\四位二进制可逆计数器_1_qb ), .QA(\四位二进制可逆计数器_1_qa ),
    .CPu(CPu), .INC(\报警电路_1_inc ), .CPd(CPd), .DEC(\报警电路_1_dec ), .ALARM(ALARM));
  \显示电路  \u_显示电路_1  (
    .D(\二进制转8421码电路_1_out_5 ), .C(\二进制转8421码电路_1_out_6 ), .a_2(out_4), .B(\二进制转8421码电路_1_out_7 ),
    .A(\二进制转8421码电路_1_out_8 ), .b_2(out_5), .c_2(out_6), .d_2(out_7), .e(out_8), .f(out_9), .g(out_10));
  \显示电路  \u_显示电路_2  (
    .D(\二进制转8421码电路_1_out_9 ), .C(\二进制转8421码电路_1_out_10 ), .a_2(out_11), .B(\二进制转8421码电路_1_out_11 ),
    .A(\二进制转8421码电路_1_out_12 ), .b_2(out_12), .c_2(out_13), .d_2(out_14), .e(out_15), .f(out_16), .g(out_17));
  \二进制转8421码电路  \u_二进制转8421码电路_1  (
    .out_5(\二进制转8421码电路_1_out_5 ), .out_6(\二进制转8421码电路_1_out_6 ), .out_7(\二进制转8421码电路_1_out_7 ),
    .out_8(\二进制转8421码电路_1_out_8 ), .out_9(\二进制转8421码电路_1_out_9 ), .out_10(\二进制转8421码电路_1_out_10 ),
    .out_11(\二进制转8421码电路_1_out_11 ), .out_12(\二进制转8421码电路_1_out_12 ), .in_1(\四位二进制可逆计数器_1_qd ),
    .in_2(\四位二进制可逆计数器_1_qc ), .in_3(\四位二进制可逆计数器_1_qb ), .in_4(\四位二进制可逆计数器_1_qa ));
  \四位二进制可逆计数器  \u_四位二进制可逆计数器_1  (
    .nLD(1'b1), .D(1'b1), .C(1'b1), .B(1'b1), .A(1'b1), .QD(\四位二进制可逆计数器_1_qd ), .QC(\四位二进制可逆计数器_1_qc ),
    .QB(\四位二进制可逆计数器_1_qb ), .QA(\四位二进制可逆计数器_1_qa ), .CLR(CLR), .CPu(\报警电路_1_inc ), .CPd(\报警电路_1_dec ));
endmodule

module \小型门禁系统测试电路  (
  input  CPu,
  input  CLR,
  input  CPd
);

  wire \小型实验室门禁系统_1_alarm , \小型实验室门禁系统_1_out_4 , \小型实验室门禁系统_1_out_5 , \小型实验室门禁系统_1_out_6 ,
       \小型实验室门禁系统_1_out_7 , \小型实验室门禁系统_1_out_8 , \小型实验室门禁系统_1_out_9 , \小型实验室门禁系统_1_out_10 ,
       \小型实验室门禁系统_1_out_11 , \小型实验室门禁系统_1_out_12 , \小型实验室门禁系统_1_out_13 , \小型实验室门禁系统_1_out_14 ,
       \小型实验室门禁系统_1_out_15 , \小型实验室门禁系统_1_out_16 , \小型实验室门禁系统_1_out_17 ;

  _7_Segment_Display #(.active("true")) u_7_segment_display_1 (
    .g(\小型实验室门禁系统_1_out_10 ), .f(\小型实验室门禁系统_1_out_9 ), .a(\小型实验室门禁系统_1_out_4 ), .b(\小型实验室门禁系统_1_out_5 ),
    .e(\小型实验室门禁系统_1_out_8 ), .d(\小型实验室门禁系统_1_out_7 ), .c(\小型实验室门禁系统_1_out_6 ));  // open: dp
  _7_Segment_Display #(.active("true")) u_7_segment_display_2 (
    .g(\小型实验室门禁系统_1_out_17 ), .f(\小型实验室门禁系统_1_out_16 ), .a(\小型实验室门禁系统_1_out_11 ), .b(\小型实验室门禁系统_1_out_12 ),
    .e(\小型实验室门禁系统_1_out_15 ), .d(\小型实验室门禁系统_1_out_14 ), .c(\小型实验室门禁系统_1_out_13 ));  // open: dp
  \小型实验室门禁系统  \u_小型实验室门禁系统_1  (
    .CPu(CPu), .CLR(CLR), .CPd(CPd), .ALARM(\小型实验室门禁系统_1_alarm ), .out_4(\小型实验室门禁系统_1_out_4 ),
    .out_5(\小型实验室门禁系统_1_out_5 ), .out_6(\小型实验室门禁系统_1_out_6 ), .out_7(\小型实验室门禁系统_1_out_7 ),
    .out_8(\小型实验室门禁系统_1_out_8 ), .out_9(\小型实验室门禁系统_1_out_9 ), .out_10(\小型实验室门禁系统_1_out_10 ),
    .out_11(\小型实验室门禁系统_1_out_11 ), .out_12(\小型实验室门禁系统_1_out_12 ), .out_13(\小型实验室门禁系统_1_out_13 ),
    .out_14(\小型实验室门禁系统_1_out_14 ), .out_15(\小型实验室门禁系统_1_out_15 ), .out_16(\小型实验室门禁系统_1_out_16 ),
    .out_17(\小型实验室门禁系统_1_out_17 ));
  LED #(.active("true")) ALARM (.in(\小型实验室门禁系统_1_alarm ));
endmodule

module \先行进位并行加法器  (
  input  A3,
  input  B3,
  input  A2,
  input  B2,
  input  A1,
  input  B1,
  input  A0,
  input  B0,
  input  C0,
  output C4,
  output S3,
  output S2,
  output S1,
  output S0
);

  wire and_1_out, and_2_out, and_3_out, and_4_out, and_5_out, and_6_out, and_7_out, and_8_out, and_9_out,
       and_10_out, G0_out, G1_out, G2_out, G3_out, or_2_out, or_3_out, or_4_out, P0_out, P1_out, P2_out,
       P3_out;

  xor P3 (P3_out, A3, B3);
  and G3 (G3_out, A3, B3);
  xor P2 (P2_out, A2, B2);
  and G2 (G2_out, A2, B2);
  xor P1 (P1_out, A1, B1);
  and G1 (G1_out, A1, B1);
  xor P0 (P0_out, A0, B0);
  and G0 (G0_out, A0, B0);
  and and_1 (and_1_out, G0_out, P1_out, P2_out, P3_out);
  and and_2 (and_2_out, P0_out, C0, P3_out, P1_out, P2_out);
  and and_3 (and_3_out, P3_out, P2_out, G1_out);
  and and_4 (and_4_out, P3_out, G2_out);
  and and_5 (and_5_out, P1_out, P2_out, G0_out);
  and and_6 (and_6_out, P1_out, P2_out, P0_out, C0);
  and and_7 (and_7_out, P2_out, G1_out);
  and and_8 (and_8_out, P1_out, G0_out);
  and and_9 (and_9_out, P1_out, P0_out, C0);
  and and_10 (and_10_out, P0_out, C0);
  or or_1 (C4, and_1_out, and_2_out, G3_out, and_3_out, and_4_out);
  or or_2 (or_2_out, and_5_out, and_6_out, G2_out, and_7_out);
  or or_3 (or_3_out, and_9_out, and_8_out, G1_out);
  or or_4 (or_4_out, and_10_out, G0_out);
  xor xor_1 (S3, P3_out, or_2_out);
  xor xor_2 (S2, P2_out, or_3_out);
  xor xor_3 (S1, P1_out, or_4_out);
  xor xor_4 (S0, P0_out, C0);
endmodule
