// Logisim project Lab3.circ as structural Verilog: 7 circuits, main circuit 四位乘法器
module \四位乘法器  (
  input  [3:0] in_1,
  input  [3:0] in_2,
  output [7:0] out_3
);

  wire bitselector_1_out, bitselector_2_out, bitselector_3_out, bitselector_4_out;
  wire [7:0] adder_1_out, adder_2_out, adder_3_out, adder_4_out, bit_extender_1_out, bit_extender_2_out,
       multiplexer_1_out, multiplexer_2_out, multiplexer_3_out, shifter_1_out, shifter_2_out, shifter_3_out;

  assign bit_extender_1_out = {{4{1'b0}}, in_1};  // Bit_Extender bit_extender_1
  assign bit_extender_2_out = {{4{1'b0}}, in_2};  // Bit_Extender bit_extender_2
  BitSelector #(.width(8), .group(1)) bitselector_1 (.in(bit_extender_1_out), .out(bitselector_1_out), .sel(3'b000));
  Adder #(.width(8)) adder_1 (.a({8{1'b0}}), .b(bit_extender_2_out), .out(adder_1_out));  // open: cin, cout
  Multiplexer #(.select(1), .width(8), .disabled("Z"), .enable("false")) multiplexer_1 (
    .in0({8{1'b0}}), .in1(adder_1_out), .out(multiplexer_1_out), .sel(bitselector_1_out));
  Shifter #(.width(8), .shift("ll")) shifter_1 (.in(bit_extender_2_out), .\dist (3'b001), .out(shifter_1_out));
  Adder #(.width(8)) adder_2 (.a(multiplexer_1_out), .b(shifter_1_out), .out(adder_2_out));  // open: cin, cout
  BitSelector #(.width(8), .group(1)) bitselector_2 (.in(bit_extender_1_out), .out(bitselector_2_out), .sel(3'b001));
  Multiplexer #(.select(1), .width(8), .disabled("Z"), .enable("false")) multiplexer_2 (
    .in0(multiplexer_1_out), .in1(adder_2_out), .out(multiplexer_2_out), .sel(bitselector_2_out));
  Shifter #(.width(8), .shift("ll")) shifter_2 (.in(shifter_1_out), .\dist (3'b001), .out(shifter_2_out));
  Adder #(.width(8)) adder_3 (.a(multiplexer_2_out), .b(shifter_2_out), .out(adder_3_out));  // open: cin, cout
  BitSelector #(.width(8), .group(1)) bitselector_3 (.in(bit_extender_1_out), .out(bitselector_3_out), .sel(3'b010));
  Multiplexer #(.select(1), .width(8), .disabled("Z"), .enable("false")) multiplexer_3 (
    .in0(multiplexer_2_out), .in1(adder_3_out), .out(multiplexer_3_out), .sel(bitselector_3_out));
  Shifter #(.width(8), .shift("ll")) shifter_3 (.in(shifter_2_out), .\dist (3'b001), .out(shifter_3_out));
  Adder #(.width(8)) adder_4 (.a(multiplexer_3_out), .b(shifter_3_out), .out(adder_4_out));  // open: cin, cout
  BitSelector #(.width(8), .group(1)) bitselector_4 (.in(bit_extender_1_out), .out(bitselector_4_out), .sel(3'b011));
  Multiplexer #(.select(1), .width(8), .disabled("Z"), .enable("false")) multiplexer_4 (
    .in0(multiplexer_3_out), .in1(adder_4_out), .out(out_3), .sel(bitselector_4_out));
endmodule

module \四位乘法器测试电路  (
  input  [3:0] in_1,
  input  [3:0] in_2,
  output [7:0] out_3
);

  \四位乘法器  \u_四位乘法器_1  (.in_1(in_1), .in_2(in_2), .out_3(out_3));
endmodule

module \_32X4乘法器  (
  input  [3:0] in_1,
  input  [31:0] in_2,
  output [31:0] out_3,
  output [31:0] out_4
);

  wire adder_3_cout, adder_4_cout, adder_6_cout;
  wire [31:0] adder_1_out, adder_2_out, adder_3_out, adder_4_out, bit_extender_1_out, bit_extender_2_out,
       bit_extender_3_out, multiplexer_1_out, multiplexer_2_out, multiplexer_3_out, multiplexer_4_out,
       multiplexer_5_out, multiplexer_6_out, multiplexer_7_out, shifter_1_out, shifter_2_out, shifter_3_out;

  assign bit_extender_1_out = {{31{1'b0}}, in_2[31]};  // Bit_Extender bit_extender_1
  assign bit_extender_2_out = {{30{1'b0}}, in_2[31:30]};  // Bit_Extender bit_extender_2
  assign bit_extender_3_out = {{29{1'b0}}, in_2[31:29]};  // Bit_Extender bit_extender_3
  Shifter #(.width(32), .shift("ll")) shifter_1 (.in(in_2), .\dist (5'b00011), .out(shifter_1_out));
  Shifter #(.width(32), .shift("ll")) shifter_2 (.in(in_2), .\dist (5'b00010), .out(shifter_2_out));
  Multiplexer #(.select(1), .width(32), .disabled("Z"), .enable("false")) multiplexer_1 (
    .in0({32{1'b0}}), .in1(shifter_3_out), .out(multiplexer_1_out), .sel(in_1[1]));
  Shifter #(.width(32), .shift("ll")) shifter_3 (.in(in_2), .\dist (5'b00001), .out(shifter_3_out));
  Multiplexer #(.select(1), .width(32), .disabled("Z"), .enable("false")) multiplexer_2 (
    .in0({32{1'b0}}), .in1(in_2), .out(multiplexer_2_out), .sel(in_1[0]));
  Multiplexer #(.select(1), .width(32), .disabled("Z"), .enable("false")) multiplexer_3 (
    .in0({32{1'b0}}), .in1(bit_extender_1_out), .out(multiplexer_3_out), .sel(in_1[1]));
  Multiplexer #(.select(1), .width(32), .disabled("Z"), .enable("false")) multiplexer_4 (
    .in0({32{1'b0}}), .in1(shifter_2_out), .out(multiplexer_4_out), .sel(in_1[2]));
  Multiplexer #(.select(1), .width(32), .disabled("Z"), .enable("false")) multiplexer_5 (
    .in0({32{1'b0}}), .in1(bit_extender_2_out), .out(multiplexer_5_out), .sel(in_1[2]));
  Multiplexer #(.select(1), .width(32), .disabled("Z"), .enable("false")) multiplexer_6 (
    .in0({32{1'b0}}), .in1(bit_extender_3_out), .out(multiplexer_6_out), .sel(in_1[3]));
  Multiplexer #(.select(1), .width(32), .disabled("Z"), .enable("false")) multiplexer_7 (
    .in0({32{1'b0}}), .in1(shifter_1_out), .out(multiplexer_7_out), .sel(in_1[3]));
  Adder #(.width(32)) adder_1 (
    .a({32{1'b0}}), .b(multiplexer_3_out), .out(adder_1_out), .cin(adder_4_cout));  // open: cout
  Adder #(.width(32)) adder_2 (
    .a(multiplexer_5_out), .b(multiplexer_6_out), .out(adder_2_out), .cin(adder_3_cout));  // open: cout
  Adder #(.width(32)) adder_3 (
    .a(multiplexer_7_out), .b(multiplexer_4_out), .out(adder_3_out), .cout(adder_3_cout));  // open: cin
  Adder #(.width(32)) adder_4 (
    .a(multiplexer_1_out), .b(multiplexer_2_out), .out(adder_4_out), .cout(adder_4_cout));  // open: cin
  Adder #(.width(32)) adder_5 (.a(adder_1_out), .b(adder_2_out), .out(out_3), .cin(adder_6_cout));  // open: cout
  Adder #(.width(32)) adder_6 (.a(adder_3_out), .b(adder_4_out), .out(out_4), .cout(adder_6_cout));  // open: cin
endmodule

module \_32X4乘法器测试电路  (
  input  [3:0] in_1,
  input  [31:0] in_2,
  output [31:0] out_3,
  output [31:0] out_4
);

  \_32X4乘法器  \u_32x4乘法器_1  (.in_1(in_1), .out_3(out_3), .in_2(in_2), .out_4(out_4));
endmodule

module \_32X32乘法器  (
  input  [31:0] in_1,
  input  [31:0] in_2,
  output [31:0] out_3,
  output [31:0] out_4
);

  wire adder_2_cout, adder_4_cout, adder_6_cout, adder_8_cout, adder_10_cout, adder_12_cout, adder_14_cout;
  wire [3:0] bitselector_1_out, bitselector_2_out, bitselector_3_out, bitselector_4_out, bitselector_5_out,
       bitselector_6_out, bitselector_7_out, bitselector_8_out;
  wire [31:0] adder_1_out, adder_2_out, adder_3_out, adder_4_out, adder_5_out, adder_6_out, adder_7_out,
       adder_8_out, adder_9_out, adder_10_out, adder_11_out, adder_12_out, \n32x4乘法器_1_out_3 ,
       \n32x4乘法器_1_out_4 , \n32x4乘法器_2_out_3 , \n32x4乘法器_2_out_4 , \n32x4乘法器_3_out_3 , \n32x4乘法器_3_out_4 ,
       \n32x4乘法器_4_out_3 , \n32x4乘法器_4_out_4 , \n32x4乘法器_5_out_3 , \n32x4乘法器_5_out_4 , \n32x4乘法器_6_out_3 ,
       \n32x4乘法器_6_out_4 , \n32x4乘法器_7_out_3 , \n32x4乘法器_7_out_4 , \n32x4乘法器_8_out_3 , \n32x4乘法器_8_out_4 ,
       \n64位4位移位器_1_out_3 , \n64位4位移位器_1_out_4 , \n64位4位移位器_2_out_3 , \n64位4位移位器_2_out_4 ,
       \n64位4位移位器_3_out_3 , \n64位4位移位器_3_out_4 , \n64位4位移位器_4_out_3 , \n64位4位移位器_4_out_4 ,
       \n64位4位移位器_5_out_3 , \n64位4位移位器_5_out_4 , \n64位4位移位器_6_out_3 , \n64位4位移位器_6_out_4 ,
       \n64位4位移位器_7_out_3 , \n64位4位移位器_7_out_4 , \n64位4位移位器_8_out_3 , \n64位4位移位器_8_out_4 ,
       \n64位4位移位器_9_out_3 , \n64位4位移位器_9_out_4 , \n64位4位移位器_10_out_3 , \n64位4位移位器_10_out_4 ,
       \n64位4位移位器_11_out_3 , \n64位4位移位器_11_out_4 , \n64位4位移位器_12_out_3 , \n64位4位移位器_12_out_4 ,
       \n64位4位移位器_13_out_3 , \n64位4位移位器_13_out_4 , \n64位4位移位器_14_out_3 , \n64位4位移位器_14_out_4 ,
       \n64位4位移位器_15_out_3 , \n64位4位移位器_15_out_4 , \n64位4位移位器_16_out_3 , \n64位4位移位器_16_out_4 ,
       \n64位4位移位器_17_out_3 , \n64位4位移位器_17_out_4 , \n64位4位移位器_18_out_3 , \n64位4位移位器_18_out_4 ,
       \n64位4位移位器_19_out_3 , \n64位4位移位器_19_out_4 , \n64位4位移位器_20_out_3 , \n64位4位移位器_20_out_4 ,
       \n64位4位移位器_21_out_3 , \n64位4位移位器_21_out_4 , \n64位4位移位器_22_out_3 , \n64位4位移位器_22_out_4 ,
       \n64位4位移位器_23_out_3 , \n64位4位移位器_23_out_4 , \n64位4位移位器_24_out_3 , \n64位4位移位器_24_out_4 ,
       \n64位4位移位器_25_out_3 , \n64位4位移位器_25_out_4 , \n64位4位移位器_26_out_3 , \n64位4位移位器_26_out_4 ,
       \n64位4位移位器_27_out_3 , \n64位4位移位器_27_out_4 , \n64位4位移位器_28_out_3 , \n64位4位移位器_28_out_4 ;

  BitSelector #(.width(32), .group(4)) bitselector_1 (.in(in_1), .out(bitselector_1_out), .sel(3'b111));
  BitSelector #(.width(32), .group(4)) bitselector_2 (.in(in_1), .out(bitselector_2_out), .sel(3'b110));
  BitSelector #(.width(32), .group(4)) bitselector_3 (.in(in_1), .out(bitselector_3_out), .sel(3'b101));
  BitSelector #(.width(32), .group(4)) bitselector_4 (.in(in_1), .out(bitselector_4_out), .sel(3'b100));
  BitSelector #(.width(32), .group(4)) bitselector_5 (.in(in_1), .out(bitselector_5_out), .sel(3'b011));
  BitSelector #(.width(32), .group(4)) bitselector_6 (.in(in_1), .out(bitselector_6_out), .sel(3'b010));
  BitSelector #(.width(32), .group(4)) bitselector_7 (.in(in_1), .out(bitselector_7_out), .sel(3'b001));
  BitSelector #(.width(32), .group(4)) bitselector_8 (.in(in_1), .out(bitselector_8_out), .sel(3'b000));
  \_32X4乘法器  \u_32x4乘法器_1  (
    .in_1(bitselector_1_out), .out_3(\n32x4乘法器_1_out_3 ), .in_2(in_2), .out_4(\n32x4乘法器_1_out_4 ));
  \_64位4位移位器  \u_64位4位移位器_1  (
    .in_1(\n32x4乘法器_1_out_4 ), .in_2(\n32x4乘法器_1_out_3 ), .out_3(\n64位4位移位器_1_out_3 ),
    .out_4(\n64位4位移位器_1_out_4 ));
  \_64位4位移位器  \u_64位4位移位器_2  (
    .in_1(\n64位4位移位器_1_out_3 ), .in_2(\n64位4位移位器_1_out_4 ), .out_3(\n64位4位移位器_2_out_3 ),
    .out_4(\n64位4位移位器_2_out_4 ));
  \_64位4位移位器  \u_64位4位移位器_3  (
    .in_1(\n64位4位移位器_4_out_3 ), .in_2(\n64位4位移位器_4_out_4 ), .out_3(\n64位4位移位器_3_out_3 ),
    .out_4(\n64位4位移位器_3_out_4 ));
  \_32X4乘法器  \u_32x4乘法器_2  (
    .in_1(bitselector_2_out), .out_3(\n32x4乘法器_2_out_3 ), .in_2(in_2), .out_4(\n32x4乘法器_2_out_4 ));
  \_64位4位移位器  \u_64位4位移位器_4  (
    .in_1(\n32x4乘法器_2_out_4 ), .in_2(\n32x4乘法器_2_out_3 ), .out_3(\n64位4位移位器_4_out_3 ),
    .out_4(\n64位4位移位器_4_out_4 ));
  \_32X4乘法器  \u_32x4乘法器_3  (
    .in_1(bitselector_3_out), .out_3(\n32x4乘法器_3_out_3 ), .in_2(in_2), .out_4(\n32x4乘法器_3_out_4 ));
  \_64位4位移位器  \u_64位4位移位器_5  (
    .in_1(\n32x4乘法器_3_out_4 ), .in_2(\n32x4乘法器_3_out_3 ), .out_3(\n64位4位移位器_5_out_3 ),
    .out_4(\n64位4位移位器_5_out_4 ));
  \_64位4位移位器  \u_64位4位移位器_6  (
    .in_1(\n64位4位移位器_5_out_3 ), .in_2(\n64位4位移位器_5_out_4 ), .out_3(\n64位4位移位器_6_out_3 ),
    .out_4(\n64位4位移位器_6_out_4 ));
  \_32X4乘法器  \u_32x4乘法器_4  (
    .in_1(bitselector_4_out), .out_3(\n32x4乘法器_4_out_3 ), .in_2(in_2), .out_4(\n32x4乘法器_4_out_4 ));
  \_64位4位移位器  \u_64位4位移位器_7  (
    .in_1(\n32x4乘法器_4_out_4 ), .in_2(\n32x4乘法器_4_out_3 ), .out_3(\n64位4位移位器_7_out_3 ),
    .out_4(\n64位4位移位器_7_out_4 ));
  \_64位4位移位器  \u_64位4位移位器_8  (
    .in_1(\n64位4位移位器_7_out_3 ), .in_2(\n64位4位移位器_7_out_4 ), .out_3(\n64位4位移位器_8_out_3 ),
    .out_4(\n64位4位移位器_8_out_4 ));
  \_32X4乘法器  \u_32x4乘法器_5  (
    .in_1(bitselector_5_out), .out_3(\n32x4乘法器_5_out_3 ), .in_2(in_2), .out_4(\n32x4乘法器_5_out_4 ));
  \_64位4位移位器  \u_64位4位移位器_9  (
    .in_1(\n64位4位移位器_10_out_3 ), .in_2(\n64位4位移位器_10_out_4 ), .out_3(\n64位4位移位器_9_out_3 ),
    .out_4(\n64位4位移位器_9_out_4 ));
  \_64位4位移位器  \u_64位4位移位器_10  (
    .in_1(\n32x4乘法器_5_out_4 ), .in_2(\n32x4乘法器_5_out_3 ), .out_3(\n64位4位移位器_10_out_3 ),
    .out_4(\n64位4位移位器_10_out_4 ));
  \_64位4位移位器  \u_64位4位移位器_11  (
    .in_1(\n32x4乘法器_6_out_4 ), .in_2(\n32x4乘法器_6_out_3 ), .out_3(\n64位4位移位器_11_out_3 ),
    .out_4(\n64位4位移位器_11_out_4 ));
  \_64位4位移位器  \u_64位4位移位器_12  (
    .in_1(\n64位4位移位器_11_out_3 ), .in_2(\n64位4位移位器_11_out_4 ), .out_3(\n64位4位移位器_12_out_3 ),
    .out_4(\n64位4位移位器_12_out_4 ));
  \_32X4乘法器  \u_32x4乘法器_6  (
    .in_1(bitselector_6_out), .out_3(\n32x4乘法器_6_out_3 ), .in_2(in_2), .out_4(\n32x4乘法器_6_out_4 ));
  \_64位4位移位器  \u_64位4位移位器_13  (
    .in_1(\n32x4乘法器_7_out_4 ), .in_2(\n32x4乘法器_7_out_3 ), .out_3(\n64位4位移位器_13_out_3 ),
    .out_4(\n64位4位移位器_13_out_4 ));
  \_32X4乘法器  \u_32x4乘法器_7  (
    .in_1(bitselector_7_out), .out_3(\n32x4乘法器_7_out_3 ), .in_2(in_2), .out_4(\n32x4乘法器_7_out_4 ));
  \_32X4乘法器  \u_32x4乘法器_8  (
    .in_1(bitselector_8_out), .out_3(\n32x4乘法器_8_out_3 ), .in_2(in_2), .out_4(\n32x4乘法器_8_out_4 ));
  \_64位4位移位器  \u_64位4位移位器_14  (
    .in_1(\n64位4位移位器_2_out_3 ), .in_2(\n64位4位移位器_2_out_4 ), .out_3(\n64位4位移位器_14_out_3 ),
    .out_4(\n64位4位移位器_14_out_4 ));
  \_64位4位移位器  \u_64位4位移位器_15  (
    .in_1(\n64位4位移位器_14_out_3 ), .in_2(\n64位4位移位器_14_out_4 ), .out_3(\n64位4位移位器_15_out_3 ),
    .out_4(\n64位4位移位器_15_out_4 ));
  \_64位4位移位器  \u_64位4位移位器_16  (
    .in_1(\n64位4位移位器_17_out_3 ), .in_2(\n64位4位移位器_17_out_4 ), .out_3(\n64位4位移位器_16_out_3 ),
    .out_4(\n64位4位移位器_16_out_4 ));
  \_64位4位移位器  \u_64位4位移位器_17  (
    .in_1(\n64位4位移位器_3_out_3 ), .in_2(\n64位4位移位器_3_out_4 ), .out_3(\n64位4位移位器_17_out_3 ),
    .out_4(\n64位4位移位器_17_out_4 ));
  \_64位4位移位器  \u_64位4位移位器_18  (
    .in_1(\n64位4位移位器_6_out_3 ), .in_2(\n64位4位移位器_6_out_4 ), .out_3(\n64位4位移位器_18_out_3 ),
    .out_4(\n64位4位移位器_18_out_4 ));
  \_64位4位移位器  \u_64位4位移位器_19  (
    .in_1(\n64位4位移位器_18_out_3 ), .in_2(\n64位4位移位器_18_out_4 ), .out_3(\n64位4位移位器_19_out_3 ),
    .out_4(\n64位4位移位器_19_out_4 ));
  \_64位4位移位器  \u_64位4位移位器_20  (
    .in_1(\n64位4位移位器_21_out_3 ), .in_2(\n64位4位移位器_21_out_4 ), .out_3(\n64位4位移位器_20_out_3 ),
    .out_4(\n64位4位移位器_20_out_4 ));
  \_64位4位移位器  \u_64位4位移位器_21  (
    .in_1(\n64位4位移位器_8_out_3 ), .in_2(\n64位4位移位器_8_out_4 ), .out_3(\n64位4位移位器_21_out_3 ),
    .out_4(\n64位4位移位器_21_out_4 ));
  \_64位4位移位器  \u_64位4位移位器_22  (
    .in_1(\n64位4位移位器_9_out_3 ), .in_2(\n64位4位移位器_9_out_4 ), .out_3(\n64位4位移位器_22_out_3 ),
    .out_4(\n64位4位移位器_22_out_4 ));
  \_64位4位移位器  \u_64位4位移位器_23  (
    .in_1(\n64位4位移位器_25_out_3 ), .in_2(\n64位4位移位器_25_out_4 ), .out_3(\n64位4位移位器_23_out_3 ),
    .out_4(\n64位4位移位器_23_out_4 ));
  \_64位4位移位器  \u_64位4位移位器_24  (
    .in_1(\n64位4位移位器_15_out_3 ), .in_2(\n64位4位移位器_15_out_4 ), .out_3(\n64位4位移位器_24_out_3 ),
    .out_4(\n64位4位移位器_24_out_4 ));
  \_64位4位移位器  \u_64位4位移位器_25  (
    .in_1(\n64位4位移位器_24_out_3 ), .in_2(\n64位4位移位器_24_out_4 ), .out_3(\n64位4位移位器_25_out_3 ),
    .out_4(\n64位4位移位器_25_out_4 ));
  \_64位4位移位器  \u_64位4位移位器_26  (
    .in_1(\n64位4位移位器_16_out_3 ), .in_2(\n64位4位移位器_16_out_4 ), .out_3(\n64位4位移位器_26_out_3 ),
    .out_4(\n64位4位移位器_26_out_4 ));
  \_64位4位移位器  \u_64位4位移位器_27  (
    .in_1(\n64位4位移位器_26_out_3 ), .in_2(\n64位4位移位器_26_out_4 ), .out_3(\n64位4位移位器_27_out_3 ),
    .out_4(\n64位4位移位器_27_out_4 ));
  \_64位4位移位器  \u_64位4位移位器_28  (
    .in_1(\n64位4位移位器_19_out_3 ), .in_2(\n64位4位移位器_19_out_4 ), .out_3(\n64位4位移位器_28_out_3 ),
    .out_4(\n64位4位移位器_28_out_4 ));
  Adder #(.width(32)) adder_1 (
    .a(\n64位4位移位器_23_out_4 ), .b(\n64位4位移位器_27_out_4 ), .out(adder_1_out), .cin(adder_2_cout));  // open: cout
  Adder #(.width(32)) adder_2 (
    .a(\n64位4位移位器_23_out_3 ), .b(\n64位4位移位器_27_out_3 ), .out(adder_2_out), .cout(adder_2_cout));  // open: cin
  Adder #(.width(32)) adder_3 (
    .a(\n64位4位移位器_28_out_4 ), .b(\n64位4位移位器_20_out_4 ), .out(adder_3_out), .cin(adder_4_cout));  // open: cout
  Adder #(.width(32)) adder_4 (
    .a(\n64位4位移位器_28_out_3 ), .b(\n64位4位移位器_20_out_3 ), .out(adder_4_out), .cout(adder_4_cout));  // open: cin
  Adder #(.width(32)) adder_5 (
    .a(\n64位4位移位器_22_out_4 ), .b(\n64位4位移位器_12_out_4 ), .out(adder_5_out), .cin(adder_6_cout));  // open: cout
  Adder #(.width(32)) adder_6 (
    .a(\n64位4位移位器_22_out_3 ), .b(\n64位4位移位器_12_out_3 ), .out(adder_6_out), .cout(adder_6_cout));  // open: cin
  Adder #(.width(32)) adder_7 (
    .a(\n64位4位移位器_13_out_4 ), .b(\n32x4乘法器_8_out_3 ), .out(adder_7_out), .cin(adder_8_cout));  // open: cout
  Adder #(.width(32)) adder_8 (
    .a(\n64位4位移位器_13_out_3 ), .b(\n32x4乘法器_8_out_4 ), .out(adder_8_out), .cout(adder_8_cout));  // open: cin
  Adder #(.width(32)) adder_9 (.a(adder_1_out), .b(adder_3_out), .out(adder_9_out), .cin(adder_10_cout));  // open: cout
  Adder #(.width(32)) adder_10 (
    .a(adder_2_out), .b(adder_4_out), .out(adder_10_out), .cout(adder_10_cout));  // open: cin
  Adder #(.width(32)) adder_11 (
    .a(adder_5_out), .b(adder_7_out), .out(adder_11_out), .cin(adder_12_cout));  // open: cout
  Adder #(.width(32)) adder_12 (
    .a(adder_6_out), .b(adder_8_out), .out(adder_12_out), .cout(adder_12_cout));  // open: cin
  Adder #(.width(32)) adder_13 (.a(adder_9_out), .b(adder_11_out), .out(out_3), .cin(adder_14_cout));  // open: cout
  Adder #(.width(32)) adder_14 (.a(adder_10_out), .b(adder_12_out), .out(out_4), .cout(adder_14_cout));  // open: cin
endmodule

module \_32X32乘法器测试电路  (
  input  [31:0] in_1,
  input  [31:0] in_2,
  output [31:0] out_3,
  output [31:0] out_4
);

  \_32X32乘法器  \u_32x32乘法器_1  (.in_1(in_1), .in_2(in_2), .out_4(out_4), .out_3(out_3));
endmodule

module \_64位4位移位器  (
  input  [31:0] in_1,
  input  [31:0] in_2,
  output [31:0] out_3,
  output [31:0] out_4
);


  assign out_3 = {in_1[27:0], 4'b0000};
  assign out_4 = {in_2[27:0], in_1[31:28]};
endmodule
