// Logisim project Lab4.circ as structural Verilog: 9 circuits, main circuit 四位除法器
module \四位除法器  (
  input  [3:0] n,
  input  [3:0] d,
  output [3:0] rem,
  output [3:0] quot
);

  wire comparator_1_lt, comparator_2_lt, comparator_3_lt, comparator_4_lt;
  wire [7:0] bit_extender_1_out, bit_extender_2_out, multiplexer_1_out, multiplexer_2_out, multiplexer_3_out,
       multiplexer_4_out, shifter_1_out, shifter_2_out, shifter_3_out, shifter_4_out, subtractor_1_out,
       subtractor_2_out, subtractor_3_out, subtractor_4_out;

  assign bit_extender_1_out = {{4{1'b0}}, n};  // Bit_Extender bit_extender_1
  assign bit_extender_2_out = {{4{1'b0}}, d};  // Bit_Extender bit_extender_2
  Shifter #(.width(8), .shift("ll")) shifter_1 (.in(bit_extender_2_out), .\dist (3'b011), .out(shifter_1_out));
  Subtractor #(.width(8)) subtractor_1 (
    .a(bit_extender_1_out), .b(shifter_1_out), .out(subtractor_1_out));  // open: bin, bout
  Comparator #(.width(8), .mode("unsigned")) comparator_1 (
    .a(bit_extender_1_out), .b(shifter_1_out), .lt(comparator_1_lt));  // open: gt, eq
  not not_1 (quot[3], comparator_1_lt);
  Shifter #(.width(8), .shift("lr")) shifter_2 (.in(shifter_1_out), .\dist (3'b001), .out(shifter_2_out));
  Multiplexer #(.select(1), .width(8), .disabled("Z"), .enable("false")) multiplexer_1 (
    .in0(bit_extender_1_out), .in1(subtractor_1_out), .out(multiplexer_1_out), .sel(quot[3]));
  Subtractor #(.width(8)) subtractor_2 (
    .a(multiplexer_1_out), .b(shifter_2_out), .out(subtractor_2_out));  // open: bin, bout
  Comparator #(.width(8), .mode("twosComplement")) comparator_2 (
    .a(multiplexer_1_out), .b(shifter_2_out), .lt(comparator_2_lt));  // open: gt, eq
  not not_2 (quot[2], comparator_2_lt);
  Shifter #(.width(8), .shift("lr")) shifter_3 (.in(shifter_2_out), .\dist (3'b001), .out(shifter_3_out));
  Multiplexer #(.select(1), .width(8), .disabled("Z"), .enable("false")) multiplexer_2 (
    .in0(multiplexer_1_out), .in1(subtractor_2_out), .out(multiplexer_2_out), .sel(quot[2]));
  Multiplexer #(.select(1), .width(8), .disabled("Z"), .enable("false")) multiplexer_3 (
    .in0(multiplexer_2_out), .in1(subtractor_3_out), .out(multiplexer_3_out), .sel(quot[1]));
  Subtractor #(.width(8)) subtractor_3 (
    .a(multiplexer_2_out), .b(shifter_3_out), .out(subtractor_3_out));  // open: bin, bout
  Comparator #(.width(8), .mode("twosComplement")) comparator_3 (
    .a(multiplexer_2_out), .b(shifter_3_out), .lt(comparator_3_lt));  // open: gt, eq
  not not_3 (quot[1], comparator_3_lt);
  Shifter #(.width(8), .shift("lr")) shifter_4 (.in(shifter_3_out), .\dist (3'b001), .out(shifter_4_out));
  Multiplexer #(.select(1), .width(8), .disabled("Z"), .enable("false")) multiplexer_4 (
    .in0(multiplexer_3_out), .in1(subtractor_4_out), .out(multiplexer_4_out), .sel(quot[0]));
  Subtractor #(.width(8)) subtractor_4 (
    .a(multiplexer_3_out), .b(shifter_4_out), .out(subtractor_4_out));  // open: bin, bout
  Comparator #(.width(8), .mode("twosComplement")) comparator_4 (
    .a(multiplexer_3_out), .b(shifter_4_out), .lt(comparator_4_lt));  // open: gt, eq
  not not_4 (quot[0], comparator_4_lt);
  Bit_Extender #(.in_width(8), .out_width(4), .\type ("zero")) bit_extender_3 (.in(multiplexer_4_out), .out(rem));
endmodule

module \四位除法器测试电路  (
  input  [3:0] in_1,
  input  [3:0] in_2,
  output [3:0] out_3,
  output [3:0] out_4
);

  \四位除法器  \u_四位除法器_1  (.n(in_1), .d(in_2), .rem(out_4), .quot(out_3));
endmodule

module \_32位除法器  (
  input  [31:0] in_1,
  input  [31:0] in_2,
  output [31:0] out_3,
  output [31:0] out_4
);

  wire [31:0] div1_1_out_5, div1_1_out_6, div1_1_out_8, div1_1_out_9, div1_2_out_5, div1_2_out_6,
       div1_2_out_8, div1_2_out_9, div1_3_out_5, div1_3_out_6, div1_3_out_8, div1_3_out_9, div1_4_out_5,
       div1_4_out_6, div1_4_out_8, div1_4_out_9, div1_5_out_5, div1_5_out_6, div1_5_out_8, div1_5_out_9,
       div1_6_out_5, div1_6_out_6, div1_6_out_8, div1_6_out_9, div1_7_out_5, div1_7_out_6, div1_7_out_8,
       div1_7_out_9, div1_8_out_5, div1_8_out_6, div1_8_out_8, div1_8_out_9, div1_9_out_5, div1_9_out_6,
       div1_9_out_8, div1_9_out_9, div1_10_out_5, div1_10_out_6, div1_10_out_8, div1_10_out_9, div1_11_out_5,
       div1_11_out_6, div1_11_out_8, div1_11_out_9, div1_12_out_5, div1_12_out_6, div1_12_out_8,
       div1_12_out_9, div1_13_out_5, div1_13_out_6, div1_13_out_8, div1_13_out_9, div1_14_out_5,
       div1_14_out_6, div1_14_out_8, div1_14_out_9, div1_15_out_5, div1_15_out_6, div1_15_out_8,
       div1_15_out_9, div1_16_out_5, div1_16_out_6, div1_16_out_8, div1_16_out_9, div1_17_out_5,
       div1_17_out_6, div1_17_out_8, div1_17_out_9, div1_18_out_5, div1_18_out_6, div1_18_out_8,
       div1_18_out_9, div1_19_out_5, div1_19_out_6, div1_19_out_8, div1_19_out_9, div1_20_out_5,
       div1_20_out_6, div1_20_out_8, div1_20_out_9, div1_21_out_5, div1_21_out_6, div1_21_out_8,
       div1_21_out_9, div1_22_out_5, div1_22_out_6, div1_22_out_8, div1_22_out_9, div1_23_out_5,
       div1_23_out_6, div1_23_out_8, div1_23_out_9, div1_24_out_5, div1_24_out_6, div1_24_out_8,
       div1_24_out_9, div1_25_out_5, div1_25_out_6, div1_25_out_8, div1_25_out_9, div1_26_out_5,
       div1_26_out_6, div1_26_out_8, div1_26_out_9, div1_27_out_5, div1_27_out_6, div1_27_out_8,
       div1_27_out_9, div1_28_out_5, div1_28_out_6, div1_28_out_8, div1_28_out_9, div1_29_out_5,
       div1_29_out_6, div1_29_out_8, div1_29_out_9, div1_30_out_5, div1_30_out_6, div1_30_out_8,
       div1_30_out_9, div1_31_out_5, div1_31_out_6, div1_31_out_8, div1_31_out_9;

  Div1 div1_1 (
    .in_1({32{1'b0}}), .in_2(in_1), .in_3({1'b0, in_2[31:1]}), .in_4({in_2[0], {31{1'b0}}}),
    .out_5(div1_1_out_5), .out_6(div1_1_out_6), .out_7(out_3[31]), .out_8(div1_1_out_8), .out_9(div1_1_out_9));
  Div1 div1_2 (
    .in_1(div1_31_out_5), .in_2(div1_31_out_6), .in_3(div1_31_out_8), .in_4(div1_31_out_9),
    .out_5(div1_2_out_5), .out_6(div1_2_out_6), .out_7(out_3[7]), .out_8(div1_2_out_8), .out_9(div1_2_out_9));
  Div1 div1_3 (
    .in_1(div1_29_out_5), .in_2(div1_29_out_6), .in_3(div1_29_out_8), .in_4(div1_29_out_9),
    .out_5(div1_3_out_5), .out_6(div1_3_out_6), .out_7(out_3[23]), .out_8(div1_3_out_8), .out_9(div1_3_out_9));
  Div1 div1_4 (
    .in_1(div1_30_out_5), .in_2(div1_30_out_6), .in_3(div1_30_out_8), .in_4(div1_30_out_9),
    .out_5(div1_4_out_5), .out_6(div1_4_out_6), .out_7(out_3[15]), .out_8(div1_4_out_8), .out_9(div1_4_out_9));
  Div1 div1_5 (
    .in_1(div1_1_out_5), .in_2(div1_1_out_6), .in_3(div1_1_out_8), .in_4(div1_1_out_9), .out_5(div1_5_out_5),
    .out_6(div1_5_out_6), .out_7(out_3[30]), .out_8(div1_5_out_8), .out_9(div1_5_out_9));
  Div1 div1_6 (
    .in_1(div1_3_out_5), .in_2(div1_3_out_6), .in_3(div1_3_out_8), .in_4(div1_3_out_9), .out_5(div1_6_out_5),
    .out_6(div1_6_out_6), .out_7(out_3[22]), .out_8(div1_6_out_8), .out_9(div1_6_out_9));
  Div1 div1_7 (
    .in_1(div1_4_out_5), .in_2(div1_4_out_6), .in_3(div1_4_out_8), .in_4(div1_4_out_9), .out_5(div1_7_out_5),
    .out_6(div1_7_out_6), .out_7(out_3[14]), .out_8(div1_7_out_8), .out_9(div1_7_out_9));
  Div1 div1_8 (
    .in_1(div1_2_out_5), .in_2(div1_2_out_6), .in_3(div1_2_out_8), .in_4(div1_2_out_9), .out_5(div1_8_out_5),
    .out_6(div1_8_out_6), .out_7(out_3[6]), .out_8(div1_8_out_8), .out_9(div1_8_out_9));
  Div1 div1_9 (
    .in_1(div1_5_out_5), .in_2(div1_5_out_6), .in_3(div1_5_out_8), .in_4(div1_5_out_9), .out_5(div1_9_out_5),
    .out_6(div1_9_out_6), .out_7(out_3[29]), .out_8(div1_9_out_8), .out_9(div1_9_out_9));
  Div1 div1_10 (
    .in_1(div1_8_out_5), .in_2(div1_8_out_6), .in_3(div1_8_out_8), .in_4(div1_8_out_9),
    .out_5(div1_10_out_5), .out_6(div1_10_out_6), .out_7(out_3[5]), .out_8(div1_10_out_8),
    .out_9(div1_10_out_9));
  Div1 div1_11 (
    .in_1(div1_6_out_5), .in_2(div1_6_out_6), .in_3(div1_6_out_8), .in_4(div1_6_out_9),
    .out_5(div1_11_out_5), .out_6(div1_11_out_6), .out_7(out_3[21]), .out_8(div1_11_out_8),
    .out_9(div1_11_out_9));
  Div1 div1_12 (
    .in_1(div1_7_out_5), .in_2(div1_7_out_6), .in_3(div1_7_out_8), .in_4(div1_7_out_9),
    .out_5(div1_12_out_5), .out_6(div1_12_out_6), .out_7(out_3[13]), .out_8(div1_12_out_8),
    .out_9(div1_12_out_9));
  Div1 div1_13 (
    .in_1(div1_9_out_5), .in_2(div1_9_out_6), .in_3(div1_9_out_8), .in_4(div1_9_out_9),
    .out_5(div1_13_out_5), .out_6(div1_13_out_6), .out_7(out_3[28]), .out_8(div1_13_out_8),
    .out_9(div1_13_out_9));
  Div1 div1_14 (
    .in_1(div1_11_out_5), .in_2(div1_11_out_6), .in_3(div1_11_out_8), .in_4(div1_11_out_9),
    .out_5(div1_14_out_5), .out_6(div1_14_out_6), .out_7(out_3[20]), .out_8(div1_14_out_8),
    .out_9(div1_14_out_9));
  Div1 div1_15 (
    .in_1(div1_12_out_5), .in_2(div1_12_out_6), .in_3(div1_12_out_8), .in_4(div1_12_out_9),
    .out_5(div1_15_out_5), .out_6(div1_15_out_6), .out_7(out_3[12]), .out_8(div1_15_out_8),
    .out_9(div1_15_out_9));
  Div1 div1_16 (
    .in_1(div1_10_out_5), .in_2(div1_10_out_6), .in_3(div1_10_out_8), .in_4(div1_10_out_9),
    .out_5(div1_16_out_5), .out_6(div1_16_out_6), .out_7(out_3[4]), .out_8(div1_16_out_8),
    .out_9(div1_16_out_9));
  Div1 div1_17 (
    .in_1(div1_13_out_5), .in_2(div1_13_out_6), .in_3(div1_13_out_8), .in_4(div1_13_out_9),
    .out_5(div1_17_out_5), .out_6(div1_17_out_6), .out_7(out_3[27]), .out_8(div1_17_out_8),
    .out_9(div1_17_out_9));
  Div1 div1_18 (
    .in_1(div1_16_out_5), .in_2(div1_16_out_6), .in_3(div1_16_out_8), .in_4(div1_16_out_9),
    .out_5(div1_18_out_5), .out_6(div1_18_out_6), .out_7(out_3[3]), .out_8(div1_18_out_8),
    .out_9(div1_18_out_9));
  Div1 div1_19 (
    .in_1(div1_14_out_5), .in_2(div1_14_out_6), .in_3(div1_14_out_8), .in_4(div1_14_out_9),
    .out_5(div1_19_out_5), .out_6(div1_19_out_6), .out_7(out_3[19]), .out_8(div1_19_out_8),
    .out_9(div1_19_out_9));
  Div1 div1_20 (
    .in_1(div1_15_out_5), .in_2(div1_15_out_6), .in_3(div1_15_out_8), .in_4(div1_15_out_9),
    .out_5(div1_20_out_5), .out_6(div1_20_out_6), .out_7(out_3[11]), .out_8(div1_20_out_8),
    .out_9(div1_20_out_9));
  Div1 div1_21 (
    .in_1(div1_17_out_5), .in_2(div1_17_out_6), .in_3(div1_17_out_8), .in_4(div1_17_out_9),
    .out_5(div1_21_out_5), .out_6(div1_21_out_6), .out_7(out_3[26]), .out_8(div1_21_out_8),
    .out_9(div1_21_out_9));
  Div1 div1_22 (
    .in_1(div1_19_out_5), .in_2(div1_19_out_6), .in_3(div1_19_out_8), .in_4(div1_19_out_9),
    .out_5(div1_22_out_5), .out_6(div1_22_out_6), .out_7(out_3[18]), .out_8(div1_22_out_8),
    .out_9(div1_22_out_9));
  Div1 div1_23 (
    .in_1(div1_20_out_5), .in_2(div1_20_out_6), .in_3(div1_20_out_8), .in_4(div1_20_out_9),
    .out_5(div1_23_out_5), .out_6(div1_23_out_6), .out_7(out_3[10]), .out_8(div1_23_out_8),
    .out_9(div1_23_out_9));
  Div1 div1_24 (
    .in_1(div1_18_out_5), .in_2(div1_18_out_6), .in_3(div1_18_out_8), .in_4(div1_18_out_9),
    .out_5(div1_24_out_5), .out_6(div1_24_out_6), .out_7(out_3[2]), .out_8(div1_24_out_8),
    .out_9(div1_24_out_9));
  Div1 div1_25 (
    .in_1(div1_21_out_5), .in_2(div1_21_out_6), .in_3(div1_21_out_8), .in_4(div1_21_out_9),
    .out_5(div1_25_out_5), .out_6(div1_25_out_6), .out_7(out_3[25]), .out_8(div1_25_out_8),
    .out_9(div1_25_out_9));
  Div1 div1_26 (
    .in_1(div1_24_out_5), .in_2(div1_24_out_6), .in_3(div1_24_out_8), .in_4(div1_24_out_9),
    .out_5(div1_26_out_5), .out_6(div1_26_out_6), .out_7(out_3[1]), .out_8(div1_26_out_8),
    .out_9(div1_26_out_9));
  Div1 div1_27 (
    .in_1(div1_22_out_5), .in_2(div1_22_out_6), .in_3(div1_22_out_8), .in_4(div1_22_out_9),
    .out_5(div1_27_out_5), .out_6(div1_27_out_6), .out_7(out_3[17]), .out_8(div1_27_out_8),
    .out_9(div1_27_out_9));
  Div1 div1_28 (
    .in_1(div1_23_out_5), .in_2(div1_23_out_6), .in_3(div1_23_out_8), .in_4(div1_23_out_9),
    .out_5(div1_28_out_5), .out_6(div1_28_out_6), .out_7(out_3[9]), .out_8(div1_28_out_8),
    .out_9(div1_28_out_9));
  Div1 div1_29 (
    .in_1(div1_25_out_5), .in_2(div1_25_out_6), .in_3(div1_25_out_8), .in_4(div1_25_out_9),
    .out_5(div1_29_out_5), .out_6(div1_29_out_6), .out_7(out_3[24]), .out_8(div1_29_out_8),
    .out_9(div1_29_out_9));
  Div1 div1_30 (
    .in_1(div1_27_out_5), .in_2(div1_27_out_6), .in_3(div1_27_out_8), .in_4(div1_27_out_9),
    .out_5(div1_30_out_5), .out_6(div1_30_out_6), .out_7(out_3[16]), .out_8(div1_30_out_8),
    .out_9(div1_30_out_9));
  Div1 div1_31 (
    .in_1(div1_28_out_5), .in_2(div1_28_out_6), .in_3(div1_28_out_8), .in_4(div1_28_out_9),
    .out_5(div1_31_out_5), .out_6(div1_31_out_6), .out_7(out_3[8]), .out_8(div1_31_out_8),
    .out_9(div1_31_out_9));
  Div1 div1_32 (
    .in_1(div1_26_out_5), .in_2(div1_26_out_6), .in_3(div1_26_out_8), .in_4(div1_26_out_9), .out_6(out_4),
    .out_7(out_3[0]));  // open: out_5, out_8, out_9
endmodule

module \_32位除法器测试电路  (
  input  [31:0] in_1,
  input  [31:0] in_2,
  output [31:0] out_3,
  output [31:0] out_4
);

  \_32位除法器  \u_32位除法器_1  (.in_1(in_1), .out_3(out_3), .in_2(in_2), .out_4(out_4));
endmodule

module Div1 (
  input  [31:0] in_1,
  input  [31:0] in_2,
  input  [31:0] in_3,
  input  [31:0] in_4,
  output [31:0] out_5,
  output [31:0] out_6,
  output out_7,
  output [31:0] out_8,
  output [31:0] out_9
);

  wire \n64位比较器_1_out_5 ;
  wire [31:0] \n64位减法器_1_out_5 , \n64位减法器_1_out_6 ;

  \_64位减法器  \u_64位减法器_1  (
    .in_1(in_2), .in_2(in_1), .in_3(in_4), .in_4(in_3), .out_5(\n64位减法器_1_out_5 ), .out_6(\n64位减法器_1_out_6 ));
  \_64位比较器  \u_64位比较器_1  (.in_1(in_1), .in_2(in_2), .in_3(in_3), .in_4(in_4), .out_5(\n64位比较器_1_out_5 ));
  \_64位右移1位  \u_64位右移1位_1  (.in_1(in_4), .in_2(in_3), .out_3(out_9), .out_4(out_8));
  not not_1 (out_7, \n64位比较器_1_out_5 );
  \_64位2选1  \u_64位2选1_1  (
    .in_1(in_1), .in_2(in_2), .in_3(\n64位减法器_1_out_6 ), .in_4(\n64位减法器_1_out_5 ), .out_6(out_5),
    .out_7(out_6), .in_5(out_7));
endmodule

module \_64位减法器  (
  input  [31:0] in_1,
  input  [31:0] in_2,
  input  [31:0] in_3,
  input  [31:0] in_4,
  output [31:0] out_5,
  output [31:0] out_6
);

  wire subtractor_2_bout;

  Subtractor #(.width(32)) subtractor_1 (.a(in_1), .b(in_3), .out(out_5), .bin(subtractor_2_bout));  // open: bout
  Subtractor #(.width(32)) subtractor_2 (.a(in_2), .b(in_4), .out(out_6), .bout(subtractor_2_bout));  // open: bin
endmodule

module \_64位比较器  (
  input  [31:0] in_1,
  input  [31:0] in_2,
  input  [31:0] in_3,
  input  [31:0] in_4,
  output out_5
);

  wire and_1_out, comparator_1_eq, comparator_1_lt, comparator_2_lt;

  Comparator #(.width(32), .mode("unsigned")) comparator_1 (
    .a(in_1), .b(in_3), .eq(comparator_1_eq), .lt(comparator_1_lt));  // open: gt
  Comparator #(.width(32), .mode("unsigned")) comparator_2 (.a(in_2), .b(in_4), .lt(comparator_2_lt));  // open: gt, eq
  and and_1 (and_1_out, comparator_1_eq, comparator_2_lt);
  or or_1 (out_5, comparator_1_lt, and_1_out);
endmodule

module \_64位2选1  (
  input  [31:0] in_1,
  input  [31:0] in_2,
  input  [31:0] in_3,
  input  [31:0] in_4,
  input  in_5,
  output [31:0] out_6,
  output [31:0] out_7
);

  Multiplexer #(.select(1), .width(32), .disabled("Z"), .enable("false")) multiplexer_1 (
    .in0(in_2), .in1(in_4), .out(out_7), .sel(in_5));
  Multiplexer #(.select(1), .width(32), .disabled("Z"), .enable("false")) multiplexer_2 (
    .in0(in_1), .in1(in_3), .out(out_6), .sel(in_5));
endmodule

module \_64位右移1位  (
  input  [31:0] in_1,
  input  [31:0] in_2,
  output [31:0] out_3,
  output [31:0] out_4
);


  assign out_3 = {in_2[0], in_1[31:1]};
  assign out_4 = {1'b0, in_2[31:1]};
endmodule
