// Logisim project Lab5.circ as structural Verilog: 16 circuits, main circuit 四位二进制可逆计数器
module \四位二进制可逆计数器  (
  input  D,
  input  C,
  input  B,
  input  A,
  input  nLD,
  input  CPu,
  input  CPd,
  input  CLR,
  output Qbb,
  output Qcc,
  output QD,
  output QC,
  output QB,
  output QA
);

  wire and_1_out, and_2_out, and_3_out, and_4_out, and_5_out, and_6_out, and_7_out, and_8_out, and_9_out,
       and_10_out, and_11_out, and_12_out, d_ff_1_qn, d_ff_2_qn, d_ff_3_qn, d_ff_4_qn, nor_1_out, nor_2_out,
       nor_3_out, nor_4_out, not_1_out, not_2_out, not_3_out, not_4_out, not_5_out, not_6_out, not_7_out,
       or_1_out, or_2_out, or_3_out, or_4_out, or_5_out, or_6_out, or_7_out, or_8_out;

  not not_1 (not_1_out, CPd);
  not not_2 (not_2_out, nLD);
  and and_1 (and_1_out, CPu, QC, QA, QB);
  nor nor_1 (nor_1_out, not_1_out, QC, QA, QB);
  and and_2 (and_2_out, CPu, QA, QB);
  nor nor_2 (nor_2_out, not_1_out, QA, QB);
  and and_3 (and_3_out, CPu, QA);
  nor nor_3 (nor_3_out, not_1_out, QA);
  and and_4 (and_4_out, not_2_out, D);
  or or_1 (or_1_out, and_1_out, nor_1_out);
  or or_2 (or_2_out, and_2_out, nor_2_out);
  or or_3 (or_3_out, and_3_out, nor_3_out);
  or or_4 (or_4_out, CPu, CPd);
  not not_3 (not_3_out, D);
  and and_5 (and_5_out, not_3_out, not_2_out);
  D_Flip_Flop #(.trigger("falling")) d_ff_1 (
    .clk(or_1_out), .D(d_ff_1_qn), .Q(QD), .Qn(d_ff_1_qn), .preset(and_4_out), .reset(or_5_out));  // open: en
  or or_5 (or_5_out, CLR, and_5_out);
  and and_6 (and_6_out, not_2_out, C);
  D_Flip_Flop #(.trigger("falling")) d_ff_2 (
    .clk(or_2_out), .D(d_ff_2_qn), .Q(QC), .Qn(d_ff_2_qn), .preset(and_6_out), .reset(or_6_out));  // open: en
  or or_6 (or_6_out, CLR, and_8_out);
  not not_4 (not_4_out, C);
  and and_7 (and_7_out, not_2_out, B);
  and and_8 (and_8_out, not_4_out, not_2_out);
  not not_5 (not_5_out, B);
  and and_9 (and_9_out, not_5_out, not_2_out);
  D_Flip_Flop #(.trigger("falling")) d_ff_3 (
    .clk(or_3_out), .D(d_ff_3_qn), .Q(QB), .Qn(d_ff_3_qn), .preset(and_7_out), .reset(or_7_out));  // open: en
  or or_7 (or_7_out, CLR, and_9_out);
  and and_10 (and_10_out, not_2_out, A);
  or or_8 (or_8_out, CLR, and_11_out);
  not not_6 (not_6_out, A);
  and and_11 (and_11_out, not_6_out, not_2_out);
  D_Flip_Flop #(.trigger("falling")) d_ff_4 (
    .clk(or_4_out), .D(d_ff_4_qn), .Q(QA), .Qn(d_ff_4_qn), .preset(and_10_out), .reset(or_8_out));  // open: en
  nor nor_4 (nor_4_out, QD, QC, QB, QA, not_7_out);
  and and_12 (and_12_out, QD, QC, QB, QA, CPu);
  not not_7 (not_7_out, CPd);
  and and_13 (Qbb, nLD, nor_4_out);
  and and_14 (Qcc, nLD, and_12_out);
endmodule

module \六十进制计数器  (
  input  Clr,
  input  CPu,
  input  Adj,
  input  CPd,
  output Q1D,
  output Q1C,
  output Q1B,
  output Q1A,
  output Q0D,
  output Q0C,
  output Q0B,
  output Q0A,
  output nQcc
);

  wire and_1_out, and_2_out, and_3_out, or_1_out, or_2_out, \四位二进制可逆计数器_1_qa , \四位二进制可逆计数器_1_qb ,
       \四位二进制可逆计数器_1_qbb , \四位二进制可逆计数器_1_qc , \四位二进制可逆计数器_1_qcc , \四位二进制可逆计数器_1_qd , \四位二进制可逆计数器_2_qa ,
       \四位二进制可逆计数器_2_qb , \四位二进制可逆计数器_2_qc , \四位二进制可逆计数器_2_qd ;

  and and_1 (and_1_out, CPu, Adj);
  and and_2 (and_2_out, Adj, or_1_out, CPd);
  or or_1 (or_1_out, \四位二进制可逆计数器_2_qd , \四位二进制可逆计数器_2_qc , \四位二进制可逆计数器_2_qb , \四位二进制可逆计数器_2_qa , \四位二进制可逆计数器_1_qa , \四位二进制可逆计数器_1_qb , \四位二进制可逆计数器_1_qc , \四位二进制可逆计数器_1_qd );
  not not_1 (nQcc, and_3_out);
  or or_2 (or_2_out, Clr, and_3_out);
  and and_3 (and_3_out, \四位二进制可逆计数器_1_qc , \四位二进制可逆计数器_1_qd , \四位二进制可逆计数器_2_qa , \四位二进制可逆计数器_2_qb );
  \四位二进制可逆计数器  \u_四位二进制可逆计数器_1  (
    .nLD(1'b1), .CPu(and_1_out), .CPd(and_2_out), .D(1'b1), .C(1'b1), .B(1'b1), .A(1'b1),
    .QD(\四位二进制可逆计数器_1_qd ), .QC(\四位二进制可逆计数器_1_qc ), .QB(\四位二进制可逆计数器_1_qb ), .QA(\四位二进制可逆计数器_1_qa ),
    .CLR(or_2_out), .Qbb(\四位二进制可逆计数器_1_qbb ), .Qcc(\四位二进制可逆计数器_1_qcc ));
  \_8位二进制数转BCD码  \u_8位二进制数转bcd码_1  (
    .in_1(\四位二进制可逆计数器_2_qd ), .in_2(\四位二进制可逆计数器_2_qc ), .in_3(\四位二进制可逆计数器_2_qb ), .in_4(\四位二进制可逆计数器_2_qa ),
    .in_5(\四位二进制可逆计数器_1_qd ), .in_6(\四位二进制可逆计数器_1_qc ), .in_7(\四位二进制可逆计数器_1_qb ), .in_8(\四位二进制可逆计数器_1_qa ),
    .out_13(Q1D), .out_14(Q1C), .out_15(Q1B), .out_16(Q1A), .out_17(Q0D), .out_18(Q0C), .out_19(Q0B),
    .out_20(Q0A));  // open: out_9, out_10, out_11, out_12
  \四位二进制可逆计数器  \u_四位二进制可逆计数器_2  (
    .nLD(1'b1), .CPu(\四位二进制可逆计数器_1_qcc ), .CPd(\四位二进制可逆计数器_1_qbb ), .D(1'b1), .C(1'b1), .B(1'b1), .A(1'b1),
    .QD(\四位二进制可逆计数器_2_qd ), .QC(\四位二进制可逆计数器_2_qc ), .QB(\四位二进制可逆计数器_2_qb ), .QA(\四位二进制可逆计数器_2_qa ),
    .CLR(or_2_out));  // open: Qbb, Qcc
endmodule

module \六十进制计数器测试电路  (
  input  in_1,
  input  in_2,
  output out_3,
  output out_4,
  output out_5,
  output out_6,
  output out_7,
  output out_8,
  output out_9,
  output out_10,
  output out_11
);

  wire button_1_out, button_2_out;

  Button button_1 (.out(button_1_out));
  Button button_2 (.out(button_2_out));
  \六十进制计数器  \u_六十进制计数器_1  (
    .Clr(in_2), .CPu(button_1_out), .CPd(button_2_out), .nQcc(out_11), .Q1D(out_3), .Q1C(out_4), .Q1B(out_5),
    .Q1A(out_6), .Q0D(out_7), .Q0C(out_8), .Q0B(out_9), .Q0A(out_10), .Adj(in_1));
endmodule

module \十二进制计数器或二十四进制的计数器电路  (
  input  Set,
  input  Clr,
  input  CPu,
  input  Adj,
  input  CPd,
  output out_6,
  output Q1D,
  output Q1C,
  output Q1B,
  output Q1A,
  output Q0D,
  output Q0C,
  output Q0B,
  output Q0A,
  output nQcc
);

  wire and_1_out, and_2_out, and_3_out, and_5_out, not_2_out, or_1_out, or_2_out, or_3_out, or_4_out,
       \四位二进制可逆计数器_1_qbb , \四位二进制可逆计数器_1_qcc ;
  wire [7:0] adder_1_out, multiplexer_1_out, \四位二进制可逆计数器_1_qa ;

  or or_1 (or_1_out, \四位二进制可逆计数器_1_qa [7], \四位二进制可逆计数器_1_qa [6], \四位二进制可逆计数器_1_qa [5], \四位二进制可逆计数器_1_qa [4], \四位二进制可逆计数器_1_qa [0], \四位二进制可逆计数器_1_qa [1], \四位二进制可逆计数器_1_qa [2], \四位二进制可逆计数器_1_qa [3]);
  not not_1 (nQcc, and_3_out);
  or or_2 (or_2_out, Clr, and_3_out);
  and and_1 (and_1_out, CPu, Adj);
  and and_2 (and_2_out, Adj, or_1_out, CPd);
  not not_2 (not_2_out, Set);
  and and_3 (and_3_out, \四位二进制可逆计数器_1_qa [3], \四位二进制可逆计数器_1_qa [4]);
  \四位二进制可逆计数器  \u_四位二进制可逆计数器_1  (
    .nLD(1'b1), .CPu(and_1_out), .CPd(and_2_out), .D(1'b1), .C(1'b1), .B(1'b1), .A(1'b1),
    .QD(\四位二进制可逆计数器_1_qa [3]), .QC(\四位二进制可逆计数器_1_qa [2]), .QB(\四位二进制可逆计数器_1_qa [1]),
    .QA(\四位二进制可逆计数器_1_qa [0]), .CLR(or_2_out), .Qbb(\四位二进制可逆计数器_1_qbb ), .Qcc(\四位二进制可逆计数器_1_qcc ));
  or or_3 (or_3_out, \四位二进制可逆计数器_1_qa [7], \四位二进制可逆计数器_1_qa [6], \四位二进制可逆计数器_1_qa [5], \四位二进制可逆计数器_1_qa [4]);
  and and_4 (out_6, not_2_out, or_4_out);
  or or_4 (or_4_out, or_3_out, and_5_out);
  and and_5 (and_5_out, \四位二进制可逆计数器_1_qa [3], \四位二进制可逆计数器_1_qa [2]);
  \四位二进制可逆计数器  \u_四位二进制可逆计数器_2  (
    .nLD(1'b1), .CPu(\四位二进制可逆计数器_1_qcc ), .CPd(\四位二进制可逆计数器_1_qbb ), .D(1'b1), .C(1'b1), .B(1'b1), .A(1'b1),
    .QD(\四位二进制可逆计数器_1_qa [7]), .QC(\四位二进制可逆计数器_1_qa [6]), .QB(\四位二进制可逆计数器_1_qa [5]),
    .QA(\四位二进制可逆计数器_1_qa [4]), .CLR(or_2_out));  // open: Qbb, Qcc
  \_8位二进制数转BCD码  \u_8位二进制数转bcd码_1  (
    .in_1(multiplexer_1_out[7]), .in_2(multiplexer_1_out[6]), .in_3(multiplexer_1_out[5]),
    .in_4(multiplexer_1_out[4]), .in_5(multiplexer_1_out[3]), .in_6(multiplexer_1_out[2]),
    .in_7(multiplexer_1_out[1]), .in_8(multiplexer_1_out[0]), .out_13(Q1D), .out_14(Q1C), .out_15(Q1B),
    .out_16(Q1A), .out_17(Q0D), .out_18(Q0C), .out_19(Q0B), .out_20(Q0A));  // open: out_9, out_10, out_11, out_12
  Multiplexer #(.width(8), .enable("false")) multiplexer_1 (
    .in0(\四位二进制可逆计数器_1_qa ), .in1(adder_1_out), .out(multiplexer_1_out), .sel(out_6));
  Adder adder_1 (.a(\四位二进制可逆计数器_1_qa ), .b(8'hf4), .out(adder_1_out));  // open: cin, cout
endmodule

module \十二进制计数器或二十四进制的计数器测试电路  (
  input  in_1,
  input  in_2,
  input  in_3,
  output out_4,
  output out_5,
  output out_6,
  output out_7,
  output out_8,
  output out_9,
  output out_10,
  output out_11,
  output out_12
);

  wire button_1_out, button_2_out;

  Button button_1 (.out(button_1_out));
  Button button_2 (.out(button_2_out));
  \十二进制计数器或二十四进制的计数器电路  \u_十二进制计数器或二十四进制的计数器电路_1  (
    .Clr(in_3), .CPu(button_1_out), .CPd(button_2_out), .nQcc(out_12), .Set(in_2), .Q1D(out_4), .Q1C(out_5),
    .Q1B(out_6), .Q1A(out_7), .Q0D(out_8), .Q0C(out_9), .Q0B(out_10), .Q0A(out_11), .Adj(in_1));  // open: out_6
endmodule

module \上下午文字显示的电路  (
  input  AM_PM,
  input  TT,
  output [4:0] out_3,
  output [4:0] out_4,
  output [4:0] out_5,
  output [4:0] out_6
);

  wire [4:0] multiplexer_1_out, multiplexer_2_out;

  Multiplexer #(.width(5), .enable("false")) multiplexer_1 (
    .in0(5'b00001), .in1(5'b10000), .out(multiplexer_1_out), .sel(AM_PM));
  Multiplexer #(.width(5), .enable("false")) multiplexer_2 (
    .in0(5'b00101), .in1(5'b10100), .out(multiplexer_2_out), .sel(AM_PM));
  Multiplexer #(.width(5), .enable("false")) multiplexer_3 (
    .in0({5{1'b0}}), .in1(multiplexer_1_out), .out(out_3), .sel(TT));
  Multiplexer #(.width(5), .enable("false")) multiplexer_4 (.in0({5{1'b0}}), .in1({5{1'b1}}), .out(out_4), .sel(TT));
  Multiplexer #(.width(5), .enable("false")) multiplexer_5 (
    .in0({5{1'b0}}), .in1(multiplexer_2_out), .out(out_5), .sel(TT));

  assign out_6 = out_3;
endmodule

module \上下午文字显示测试电路  (
  input  in_1,
  input  in_2
);

  wire [4:0] \上下午文字显示的电路_1_out_3 , \上下午文字显示的电路_1_out_4 , \上下午文字显示的电路_1_out_5 , \上下午文字显示的电路_1_out_6 ;

  DotMatrix #(.matrixcols(4), .matrixrows(5)) dotmatrix_1 (
    .col0(\上下午文字显示的电路_1_out_3 ), .col1(\上下午文字显示的电路_1_out_4 ), .col2(\上下午文字显示的电路_1_out_5 ),
    .col3(\上下午文字显示的电路_1_out_6 ));
  \上下午文字显示的电路  \u_上下午文字显示的电路_1  (
    .out_3(\上下午文字显示的电路_1_out_3 ), .out_4(\上下午文字显示的电路_1_out_4 ), .out_5(\上下午文字显示的电路_1_out_5 ),
    .out_6(\上下午文字显示的电路_1_out_6 ), .AM_PM(in_1), .TT(in_2));
endmodule

module \电子钟整点报时电路  (
  input  in_1,
  input  [3:0] min1,
  input  [3:0] min0,
  input  [3:0] sec1,
  input  [3:0] sec0,
  output out_6
);

  and and_1 (out_6, min1[0], min1[2], in_1, min0[0], min0[3], sec1[0], sec1[2]);
endmodule

module \电子钟整点报时电路测试电路  (
  input  in_1,
  input  [3:0] in_2,
  input  [3:0] in_3,
  input  [3:0] in_4,
  input  [3:0] in_5,
  output out_6
);

  \电子钟整点报时电路  \u_电子钟整点报时电路_1  (.in_1(in_1), .min1(in_2), .min0(in_3), .sec1(in_4), .sec0(in_5), .out_6(out_6));
endmodule

module \秒脉冲产生电路  (
  output out_1
);

  wire clock_1_out, d_ff_1_qn, \四位二进制可逆计数器_1_qc ;

  Clock clock_1 (.out(clock_1_out));
  D_Flip_Flop #(.trigger("falling")) d_ff_1 (
    .clk(\四位二进制可逆计数器_1_qc ), .D(d_ff_1_qn), .Q(out_1), .Qn(d_ff_1_qn));  // open: preset, en, reset
  \四位二进制可逆计数器  \u_四位二进制可逆计数器_1  (
    .nLD(1'b1), .CPu(clock_1_out), .CPd(1'b0), .D(1'b1), .C(1'b1), .B(1'b1), .A(1'b1),
    .QC(\四位二进制可逆计数器_1_qc ), .CLR(\四位二进制可逆计数器_1_qc ));  // open: QD, QB, QA, Qbb, Qcc
endmodule

module \多功能数字钟  (
  input  Alarm,
  input  AlarmClr,
  input  in_3,
  input  CPu,
  input  CPd,
  input  Adj1,
  input  Adj0,
  input  in_8,
  input  Set,
  input  Clr,
  output [3:0] out_11,
  output [3:0] out_12,
  output [3:0] out_13,
  output Alarm_2,
  output [3:0] out_15,
  output out_16,
  output [4:0] out_17,
  output [4:0] out_18,
  output [4:0] out_19,
  output [4:0] out_20,
  output [3:0] out_21,
  output [3:0] out_22
);

  wire and_1_out, and_2_out, and_3_out, and_4_out, and_5_out, and_6_out, and_7_out, and_8_out, and_9_out,
       comparator_1_eq, not_1_out, not_2_out, not_3_out, not_4_out, not_5_out, or_1_out, or_2_out,
       \六十进制计数器_1_nqcc , \六十进制计数器_2_nqcc , \十二进制计数器或二十四进制的计数器电路_1_out_6 , \秒脉冲产生电路_1_out_1 ;
  wire [3:0] multiplexer_5_out, multiplexer_6_out, nor_1_out, \六十进制计数器_1_q0a , \六十进制计数器_1_q1a ,
       \六十进制计数器_2_q0a , \六十进制计数器_2_q1a , \十二进制计数器或二十四进制的计数器电路_1_q0a , \十二进制计数器或二十四进制的计数器电路_1_q1a ,
       \闹钟_1_out_15 , \闹钟_1_out_16 , \闹钟_1_out_17 , \闹钟_1_out_18 ;
  wire [4:0] \闹钟_1_out_19 , \闹钟_1_out_20 , \闹钟_1_out_21 , \闹钟_1_out_22 ;
  wire [19:0] \上下午文字显示的电路_1_out_6 ;

  not not_1 (not_1_out, Alarm);
  and and_1 (and_1_out, CPd, Alarm, Adj0);
  and and_2 (and_2_out, Adj0, not_1_out, not_2_out);
  not not_2 (not_2_out, Adj1);
  and and_3 (and_3_out, Adj1, not_1_out, Adj0);
  Multiplexer #(.width(4), .enable("false")) multiplexer_1 (
    .in0(\六十进制计数器_1_q1a ), .in1(4'b0000), .out(out_21), .sel(Alarm));
  \秒脉冲产生电路  \u_秒脉冲产生电路_1  (.out_1(\秒脉冲产生电路_1_out_1 ));
  and and_4 (and_4_out, CPu, Alarm, Adj0);
  Multiplexer #(.width(4), .enable("false")) multiplexer_2 (
    .in0(\六十进制计数器_1_q0a ), .in1(4'b0000), .out(out_22), .sel(Alarm));
  and and_5 (and_5_out, CPu, and_3_out);
  and and_6 (and_6_out, CPd, and_3_out);
  \六十进制计数器  \u_六十进制计数器_1  (
    .Clr(Clr), .CPu(\秒脉冲产生电路_1_out_1 ), .CPd(1'b0), .nQcc(\六十进制计数器_1_nqcc ), .Q1D(\六十进制计数器_1_q1a [3]),
    .Q1C(\六十进制计数器_1_q1a [2]), .Q1B(\六十进制计数器_1_q1a [1]), .Q1A(\六十进制计数器_1_q1a [0]), .Q0D(\六十进制计数器_1_q0a [3]),
    .Q0C(\六十进制计数器_1_q0a [2]), .Q0B(\六十进制计数器_1_q0a [1]), .Q0A(\六十进制计数器_1_q0a [0]), .Adj(1'b1));
  \电子钟整点报时电路  \u_电子钟整点报时电路_1  (
    .in_1(\秒脉冲产生电路_1_out_1 ), .min1(\六十进制计数器_2_q1a ), .min0(\六十进制计数器_2_q0a ), .sec1(\六十进制计数器_1_q1a ),
    .sec0(\六十进制计数器_1_q0a ), .out_6(out_16));
  not not_3 (not_3_out, \六十进制计数器_1_nqcc );
  \闹钟  \u_闹钟_1  (
    .min1(\六十进制计数器_2_q1a ), .min0(\六十进制计数器_2_q0a ), .hour1(\十二进制计数器或二十四进制的计数器电路_1_q1a ),
    .hour0(\十二进制计数器或二十四进制的计数器电路_1_q0a ), .out_15(\闹钟_1_out_15 ), .out_16(\闹钟_1_out_16 ),
    .out_17(\闹钟_1_out_17 ), .out_18(\闹钟_1_out_18 ), .CPu(and_4_out), .CPd(and_1_out), .Adj1(Adj1),
    .Alarm(Alarm_2), .out_19(\闹钟_1_out_19 ), .out_20(\闹钟_1_out_20 ), .out_21(\闹钟_1_out_21 ),
    .out_22(\闹钟_1_out_22 ), .Clr(AlarmClr), .Set(Set), .sec1(\六十进制计数器_1_q1a ), .sec0(\六十进制计数器_1_q0a ),
    .A_P(\十二进制计数器或二十四进制的计数器电路_1_out_6 ), .On_Off(in_3));
  or or_1 (or_1_out, and_5_out, not_3_out);
  and and_7 (and_7_out, CPu, and_2_out);
  and and_8 (and_8_out, CPd, and_2_out);
  \六十进制计数器  \u_六十进制计数器_2  (
    .Clr(Clr), .CPu(or_1_out), .CPd(and_6_out), .nQcc(\六十进制计数器_2_nqcc ), .Q1D(\六十进制计数器_2_q1a [3]),
    .Q1C(\六十进制计数器_2_q1a [2]), .Q1B(\六十进制计数器_2_q1a [1]), .Q1A(\六十进制计数器_2_q1a [0]), .Q0D(\六十进制计数器_2_q0a [3]),
    .Q0C(\六十进制计数器_2_q0a [2]), .Q0B(\六十进制计数器_2_q0a [1]), .Q0A(\六十进制计数器_2_q0a [0]), .Adj(1'b1));
  Multiplexer #(.width(4), .enable("false")) multiplexer_3 (
    .in0(\六十进制计数器_2_q1a ), .in1(\闹钟_1_out_15 ), .out(out_11), .sel(Alarm));
  Multiplexer #(.width(4), .enable("false")) multiplexer_4 (
    .in0(\六十进制计数器_2_q0a ), .in1(\闹钟_1_out_16 ), .out(out_12), .sel(Alarm));
  not not_4 (not_4_out, \六十进制计数器_2_nqcc );
  or or_2 (or_2_out, and_7_out, not_4_out);
  Multiplexer #(.width(4), .enable("false")) multiplexer_5 (
    .in0(\十二进制计数器或二十四进制的计数器电路_1_q1a ), .in1(\闹钟_1_out_17 ), .out(multiplexer_5_out), .sel(Alarm));
  assign nor_1_out = ~(\十二进制计数器或二十四进制的计数器电路_1_q1a  | \十二进制计数器或二十四进制的计数器电路_1_q0a );  // NOR_Gate nor_1, 4 bits wide
  and and_9 (and_9_out, comparator_1_eq, not_5_out);
  Comparator #(.width(4), .mode("unsigned")) comparator_1 (
    .a(4'b1111), .b(nor_1_out), .eq(comparator_1_eq));  // open: gt, lt
  Multiplexer #(.width(4), .enable("false")) multiplexer_6 (
    .in0(\十二进制计数器或二十四进制的计数器电路_1_q0a ), .in1(\闹钟_1_out_18 ), .out(multiplexer_6_out), .sel(Alarm));
  Multiplexer #(.width(4), .enable("false")) multiplexer_7 (
    .in0(multiplexer_5_out), .in1(4'b0001), .out(out_15), .sel(and_9_out));
  Multiplexer #(.width(4), .enable("false")) multiplexer_8 (
    .in0(multiplexer_6_out), .in1(4'b0010), .out(out_13), .sel(and_9_out));
  Multiplexer #(.width(20), .enable("false")) multiplexer_9 (
    .in0(\上下午文字显示的电路_1_out_6 ), .in1({\闹钟_1_out_19 , \闹钟_1_out_20 , \闹钟_1_out_21 , \闹钟_1_out_22 }),
    .out({out_17, out_18, out_19, out_20}), .sel(Alarm));
  \上下午文字显示的电路  \u_上下午文字显示的电路_1  (
    .out_3(\上下午文字显示的电路_1_out_6 [19:15]), .out_4(\上下午文字显示的电路_1_out_6 [14:10]),
    .out_5(\上下午文字显示的电路_1_out_6 [9:5]), .out_6(\上下午文字显示的电路_1_out_6 [4:0]),
    .AM_PM(\十二进制计数器或二十四进制的计数器电路_1_out_6 ), .TT(not_5_out));
  \十二进制计数器或二十四进制的计数器电路  \u_十二进制计数器或二十四进制的计数器电路_1  (
    .Clr(Clr), .CPu(or_2_out), .CPd(and_8_out), .Set(Set), .Q1D(\十二进制计数器或二十四进制的计数器电路_1_q1a [3]),
    .Q1C(\十二进制计数器或二十四进制的计数器电路_1_q1a [2]), .Q1B(\十二进制计数器或二十四进制的计数器电路_1_q1a [1]),
    .Q1A(\十二进制计数器或二十四进制的计数器电路_1_q1a [0]), .Q0D(\十二进制计数器或二十四进制的计数器电路_1_q0a [3]),
    .Q0C(\十二进制计数器或二十四进制的计数器电路_1_q0a [2]), .Q0B(\十二进制计数器或二十四进制的计数器电路_1_q0a [1]),
    .Q0A(\十二进制计数器或二十四进制的计数器电路_1_q0a [0]), .Adj(1'b1), .out_6(\十二进制计数器或二十四进制的计数器电路_1_out_6 ));  // open: nQcc
  not not_5 (not_5_out, Set);
endmodule

module \多功能数字钟测试电路  (
  input  in_1,
  input  in_2,
  input  in_3,
  input  in_4,
  input  in_5
);

  wire button_1_out, button_2_out, button_3_out, button_4_out, clock_1_out, \多功能数字钟_1_alarm_2 ,
       \多功能数字钟_1_out_16 ;
  wire [3:0] \多功能数字钟_1_out_11 , \多功能数字钟_1_out_12 , \多功能数字钟_1_out_13 , \多功能数字钟_1_out_15 , \多功能数字钟_1_out_21 ,
       \多功能数字钟_1_out_22 ;
  wire [4:0] \多功能数字钟_1_out_17 , \多功能数字钟_1_out_18 , \多功能数字钟_1_out_19 , \多功能数字钟_1_out_20 ;

  DotMatrix #(.matrixcols(4), .matrixrows(5)) dotmatrix_1 (
    .col0(\多功能数字钟_1_out_17 ), .col1(\多功能数字钟_1_out_18 ), .col2(\多功能数字钟_1_out_19 ), .col3(\多功能数字钟_1_out_20 ));
  Clock clock_1 (.out(clock_1_out));
  Hex_Digit_Display hex_digit_display_1 (.value(\多功能数字钟_1_out_15 ));  // open: dp
  Hex_Digit_Display hex_digit_display_2 (.value(\多功能数字钟_1_out_13 ));  // open: dp
  Button button_1 (.out(button_1_out));
  Button button_2 (.out(button_2_out));
  Hex_Digit_Display hex_digit_display_3 (.value(\多功能数字钟_1_out_12 ));  // open: dp
  Hex_Digit_Display hex_digit_display_4 (.value(\多功能数字钟_1_out_11 ));  // open: dp
  Button button_3 (.out(button_3_out));
  Hex_Digit_Display hex_digit_display_5 (.value(\多功能数字钟_1_out_21 ));  // open: dp
  Hex_Digit_Display hex_digit_display_6 (.value(\多功能数字钟_1_out_22 ));  // open: dp
  \多功能数字钟  \u_多功能数字钟_1  (
    .CPu(button_2_out), .CPd(button_1_out), .Adj1(in_2), .Adj0(in_1), .out_16(\多功能数字钟_1_out_16 ),
    .out_21(\多功能数字钟_1_out_21 ), .out_22(\多功能数字钟_1_out_22 ), .Clr(button_3_out), .Set(in_3),
    .out_17(\多功能数字钟_1_out_17 ), .out_18(\多功能数字钟_1_out_18 ), .out_19(\多功能数字钟_1_out_19 ),
    .out_20(\多功能数字钟_1_out_20 ), .in_8(clock_1_out), .AlarmClr(button_4_out), .Alarm_2(\多功能数字钟_1_alarm_2 ),
    .Alarm(in_4), .in_3(in_5), .out_11(\多功能数字钟_1_out_11 ), .out_12(\多功能数字钟_1_out_12 ),
    .out_15(\多功能数字钟_1_out_15 ), .out_13(\多功能数字钟_1_out_13 ));
  Button button_4 (.out(button_4_out));
  LED led_1 (.in(\多功能数字钟_1_alarm_2 ));
  LED led_2 (.in(\多功能数字钟_1_out_16 ));
endmodule

module \闹钟  (
  input  On_Off,
  input  [3:0] sec1,
  input  [3:0] sec0,
  input  [3:0] min1,
  input  [3:0] min0,
  input  [3:0] hour1,
  input  [3:0] hour0,
  input  A_P,
  input  CPu,
  input  CPd,
  input  Adj1,
  input  Clr,
  input  Set,
  output Alarm,
  output [3:0] out_15,
  output [3:0] out_16,
  output [3:0] out_17,
  output [3:0] out_18,
  output [4:0] out_19,
  output [4:0] out_20,
  output [4:0] out_21,
  output [4:0] out_22
);

  wire and_1_out, and_2_out, and_3_out, and_4_out, comparator_1_eq, comparator_2_eq, comparator_3_eq,
       comparator_4_eq, comparator_5_eq, comparator_6_eq, comparator_7_eq, not_1_out, not_2_out, or_1_out,
       xnor_1_out, \十二进制计数器或二十四进制的计数器电路_1_out_6 ;

  not not_1 (not_1_out, Adj1);
  and and_1 (and_1_out, Adj1, CPu);
  and and_2 (and_2_out, CPu, not_1_out);
  and and_3 (and_3_out, CPd, not_1_out);
  \六十进制计数器  \u_六十进制计数器_1  (
    .Clr(Clr), .CPu(and_1_out), .CPd(CPd), .Q1D(out_15[3]), .Q1C(out_15[2]), .Q1B(out_15[1]),
    .Q1A(out_15[0]), .Q0D(out_16[3]), .Q0C(out_16[2]), .Q0B(out_16[1]), .Q0A(out_16[0]), .Adj(Adj1));  // open: nQcc
  Comparator #(.width(4), .mode("unsigned")) comparator_1 (
    .a(4'b0001), .b(sec1), .eq(comparator_1_eq));  // open: gt, lt
  Comparator #(.width(4), .mode("unsigned")) comparator_2 (
    .a(sec1), .b(4'b0000), .eq(comparator_2_eq));  // open: gt, lt
  Comparator #(.width(4), .mode("unsigned")) comparator_3 (
    .a(sec0), .b(4'b0000), .eq(comparator_3_eq));  // open: gt, lt
  Comparator #(.width(4), .mode("unsigned")) comparator_4 (.a(min1), .b(out_15), .eq(comparator_4_eq));  // open: gt, lt
  Comparator #(.width(4), .mode("unsigned")) comparator_5 (.a(min0), .b(out_16), .eq(comparator_5_eq));  // open: gt, lt
  Comparator #(.width(4), .mode("unsigned")) comparator_6 (
    .a(hour1), .b(out_17), .eq(comparator_6_eq));  // open: gt, lt
  Comparator #(.width(4), .mode("unsigned")) comparator_7 (
    .a(hour0), .b(out_18), .eq(comparator_7_eq));  // open: gt, lt
  xnor xnor_1 (xnor_1_out, A_P, \十二进制计数器或二十四进制的计数器电路_1_out_6 );
  and and_4 (and_4_out, comparator_1_eq, comparator_3_eq);
  or or_1 (or_1_out, comparator_2_eq, and_4_out);
  \上下午文字显示的电路  \u_上下午文字显示的电路_1  (
    .out_3(out_19), .out_4(out_20), .out_5(out_21), .out_6(out_22), .AM_PM(\十二进制计数器或二十四进制的计数器电路_1_out_6 ),
    .TT(not_2_out));
  not not_2 (not_2_out, Set);
  \十二进制计数器或二十四进制的计数器电路  \u_十二进制计数器或二十四进制的计数器电路_1  (
    .Clr(Clr), .CPu(and_2_out), .CPd(and_3_out), .Set(Set), .Q1D(out_17[3]), .Q1C(out_17[2]),
    .Q1B(out_17[1]), .Q1A(out_17[0]), .Q0D(out_18[3]), .Q0C(out_18[2]), .Q0B(out_18[1]), .Q0A(out_18[0]),
    .Adj(not_1_out), .out_6(\十二进制计数器或二十四进制的计数器电路_1_out_6 ));  // open: nQcc
  and and_5 (Alarm, or_1_out, comparator_4_eq, comparator_5_eq, On_Off, comparator_6_eq, comparator_7_eq, xnor_1_out);
endmodule

module \闹钟测试  (
  input  in_1,
  input  Set,
  input  in_3,
  input  [3:0] in_4,
  input  [3:0] in_5,
  input  [3:0] in_6,
  input  [3:0] in_7,
  input  [3:0] in_8,
  input  [3:0] in_9,
  input  in_10
);

  wire button_1_out, button_2_out, button_3_out, \闹钟_1_alarm ;
  wire [3:0] \闹钟_1_out_15 , \闹钟_1_out_16 , \闹钟_1_out_17 , \闹钟_1_out_18 ;
  wire [4:0] \闹钟_1_out_19 , \闹钟_1_out_20 , \闹钟_1_out_21 , \闹钟_1_out_22 ;

  Button button_1 (.out(button_1_out));
  Button button_2 (.out(button_2_out));
  DotMatrix #(.matrixcols(4), .matrixrows(5)) dotmatrix_1 (
    .col0(\闹钟_1_out_19 ), .col1(\闹钟_1_out_20 ), .col2(\闹钟_1_out_21 ), .col3(\闹钟_1_out_22 ));
  Hex_Digit_Display hex_digit_display_1 (.value(\闹钟_1_out_18 ));  // open: dp
  Hex_Digit_Display hex_digit_display_2 (.value(\闹钟_1_out_17 ));  // open: dp
  Hex_Digit_Display hex_digit_display_3 (.value(\闹钟_1_out_15 ));  // open: dp
  Hex_Digit_Display hex_digit_display_4 (.value(\闹钟_1_out_16 ));  // open: dp
  \闹钟  \u_闹钟_1  (
    .min1(in_6), .min0(in_7), .hour1(in_4), .hour0(in_5), .out_15(\闹钟_1_out_15 ), .out_16(\闹钟_1_out_16 ),
    .out_17(\闹钟_1_out_17 ), .out_18(\闹钟_1_out_18 ), .CPu(button_1_out), .CPd(button_2_out), .Adj1(in_1),
    .Alarm(\闹钟_1_alarm ), .out_19(\闹钟_1_out_19 ), .out_20(\闹钟_1_out_20 ), .out_21(\闹钟_1_out_21 ),
    .out_22(\闹钟_1_out_22 ), .Clr(button_3_out), .Set(Set), .sec1(in_8), .sec0(in_9), .A_P(in_3),
    .On_Off(in_10));
  LED led_1 (.in(\闹钟_1_alarm ));
  Button button_3 (.out(button_3_out));
endmodule

module \_8位二进制数转BCD码  (
  input  in_1,
  input  in_2,
  input  in_3,
  input  in_4,
  input  in_5,
  input  in_6,
  input  in_7,
  input  in_8,
  output out_9,
  output out_10,
  output out_11,
  output out_12,
  output out_13,
  output out_14,
  output out_15,
  output out_16,
  output out_17,
  output out_18,
  output out_19,
  output out_20
);

  wire add3_1_out_5, add3_1_out_6, add3_1_out_7, add3_1_out_8, add3_2_out_5, add3_2_out_6, add3_2_out_7,
       add3_2_out_8, add3_3_out_5, add3_3_out_6, add3_3_out_7, add3_3_out_8, add3_4_out_5, add3_4_out_6,
       add3_4_out_7, add3_4_out_8, add3_5_out_6, add3_5_out_7, add3_5_out_8;

  Add3 add3_1 (
    .in_1(1'b0), .in_2(in_1), .in_3(in_2), .in_4(in_3), .out_5(add3_1_out_5), .out_6(add3_1_out_6),
    .out_7(add3_1_out_7), .out_8(add3_1_out_8));
  Add3 add3_2 (
    .in_1(add3_1_out_6), .in_2(add3_1_out_7), .in_3(add3_1_out_8), .in_4(in_4), .out_5(add3_2_out_5),
    .out_6(add3_2_out_6), .out_7(add3_2_out_7), .out_8(add3_2_out_8));
  Add3 add3_3 (
    .in_1(add3_2_out_6), .in_2(add3_2_out_7), .in_3(add3_2_out_8), .in_4(in_5), .out_5(add3_3_out_5),
    .out_6(add3_3_out_6), .out_7(add3_3_out_7), .out_8(add3_3_out_8));
  Add3 add3_4 (
    .in_1(add3_3_out_6), .in_2(add3_3_out_7), .in_3(add3_3_out_8), .in_4(in_6), .out_5(add3_4_out_5),
    .out_6(add3_4_out_6), .out_7(add3_4_out_7), .out_8(add3_4_out_8));
  Add3 add3_5 (
    .in_1(1'b0), .in_2(add3_1_out_5), .in_3(add3_2_out_5), .in_4(add3_3_out_5), .out_5(out_12),
    .out_6(add3_5_out_6), .out_7(add3_5_out_7), .out_8(add3_5_out_8));
  Add3 add3_6 (
    .in_1(add3_4_out_6), .in_2(add3_4_out_7), .in_3(add3_4_out_8), .in_4(in_7), .out_5(out_16),
    .out_6(out_17), .out_7(out_18), .out_8(out_19));
  Add3 add3_7 (
    .in_1(add3_5_out_6), .in_2(add3_5_out_7), .in_3(add3_5_out_8), .in_4(add3_4_out_5), .out_6(out_13),
    .out_7(out_14), .out_8(out_15));  // open: out_5

  assign out_9 = 1'b0;
  assign out_10 = 1'b0;
  assign out_11 = 1'b0;
  assign out_20 = in_8;
endmodule

module Add3 (
  input  in_1,
  input  in_2,
  input  in_3,
  input  in_4,
  output out_5,
  output out_6,
  output out_7,
  output out_8
);

  wire and_1_out, and_2_out, or_1_out;
  wire [3:0] adder_1_out;

  and and_1 (and_1_out, in_2, in_4);
  and and_2 (and_2_out, in_2, in_3);
  or or_1 (or_1_out, in_1, and_2_out, and_1_out);
  Adder #(.width(4)) adder_1 (.a({in_1, in_2, in_3, in_4}), .b(4'b0011), .out(adder_1_out));  // open: cin, cout
  Multiplexer #(.width(4), .enable("false")) multiplexer_1 (
    .in0({in_1, in_2, in_3, in_4}), .in1(adder_1_out), .out({out_5, out_6, out_7, out_8}), .sel(or_1_out));
endmodule
