// Logisim project Lab6.circ as structural Verilog: 9 circuits, main circuit sqrX
module sqrX (
  input  [31:0] a,
  input  [31:0] b,
  input  [31:0] c,
  input  [31:0] d,
  output [31:0] a_prime,
  output [31:0] b_prime,
  output [31:0] c_prime,
  output [31:0] d_prime
);

  wire [31:0] multiplier_1_out, multiplier_2_out, multiplier_3_out, multiplier_4_out, multiplier_5_out,
       multiplier_6_out, multiplier_7_out;

  Multiplier #(.width(32)) multiplier_1 (.a(a), .b(a), .out(multiplier_1_out), .cin({32{1'b0}}));  // open: cout
  Multiplier #(.width(32)) multiplier_2 (.a(a), .b(b), .out(multiplier_2_out), .cin({32{1'b0}}));  // open: cout
  Multiplier #(.width(32)) multiplier_3 (.a(a), .b(c), .out(multiplier_3_out), .cin({32{1'b0}}));  // open: cout
  Multiplier #(.width(32)) multiplier_4 (.a(b), .b(c), .out(multiplier_4_out), .cin({32{1'b0}}));  // open: cout
  Multiplier #(.width(32)) multiplier_5 (.a(b), .b(d), .out(multiplier_5_out), .cin({32{1'b0}}));  // open: cout
  Multiplier #(.width(32)) multiplier_6 (.a(c), .b(d), .out(multiplier_6_out), .cin({32{1'b0}}));  // open: cout
  Multiplier #(.width(32)) multiplier_7 (.a(d), .b(d), .out(multiplier_7_out), .cin({32{1'b0}}));  // open: cout
  Adder #(.width(32)) adder_1 (.a(multiplier_1_out), .b(multiplier_4_out), .out(a_prime), .cin(1'b0));  // open: cout
  Adder #(.width(32)) adder_2 (.a(multiplier_2_out), .b(multiplier_5_out), .out(b_prime), .cin(1'b0));  // open: cout
  Adder #(.width(32)) adder_3 (.a(multiplier_3_out), .b(multiplier_6_out), .out(c_prime), .cin(1'b0));  // open: cout
  Adder #(.width(32)) adder_4 (.a(multiplier_4_out), .b(multiplier_7_out), .out(d_prime), .cin(1'b0));  // open: cout
endmodule

module sqrX_A (
  input  [31:0] a,
  input  [31:0] b,
  input  [31:0] c,
  input  [31:0] d,
  output [31:0] a_prime_prime,
  output [31:0] b_prime_prime,
  output [31:0] c_prime_prime,
  output [31:0] d_prime_prime
);

  wire [31:0] sqrx_1_a_prime, sqrx_1_c_prime;

  sqrX sqrx_1 (
    .a(a), .b(b), .c(c), .d(d), .a_prime(sqrx_1_a_prime), .b_prime(a_prime_prime), .c_prime(sqrx_1_c_prime),
    .d_prime(c_prime_prime));
  Adder #(.width(32)) adder_1 (.a(sqrx_1_a_prime), .b(a_prime_prime), .out(b_prime_prime), .cin(1'b0));  // open: cout
  Adder #(.width(32)) adder_2 (.a(sqrx_1_c_prime), .b(c_prime_prime), .out(d_prime_prime), .cin(1'b0));  // open: cout
endmodule

module \Fibonacci数显示模块  (
  input  [31:0] in_1,
  output [3:0] out_2,
  output [3:0] out_3,
  output [3:0] out_4,
  output [3:0] out_5,
  output [3:0] out_6,
  output [3:0] out_7,
  output [3:0] out_8,
  output [3:0] out_9,
  output [3:0] out_10,
  output [3:0] out_11
);

  wire c_1_out_5, c_1_out_6, c_1_out_7, c_1_out_8, c_2_out_5, c_2_out_6, c_2_out_7, c_2_out_8, c_3_out_5,
       c_3_out_6, c_3_out_7, c_3_out_8, c_4_out_5, c_4_out_6, c_4_out_7, c_4_out_8, c_5_out_5, c_5_out_6,
       c_5_out_7, c_5_out_8, c_6_out_5, c_6_out_6, c_6_out_7, c_6_out_8, c_7_out_6, c_7_out_7, c_7_out_8,
       c_9_out_5, c_9_out_6, c_9_out_7, c_9_out_8, c_10_out_5, c_10_out_6, c_10_out_7, c_10_out_8,
       c_11_out_5, c_11_out_6, c_11_out_7, c_11_out_8, c_12_out_5, c_12_out_6, c_12_out_7, c_12_out_8,
       c_13_out_5, c_13_out_6, c_13_out_7, c_13_out_8, c_14_out_5, c_14_out_6, c_14_out_7, c_14_out_8,
       c_15_out_5, c_15_out_6, c_15_out_7, c_15_out_8, c_16_out_5, c_16_out_6, c_16_out_7, c_16_out_8,
       c_17_out_5, c_17_out_6, c_17_out_7, c_17_out_8, c_18_out_5, c_18_out_6, c_18_out_7, c_18_out_8,
       c_19_out_5, c_19_out_6, c_19_out_7, c_19_out_8, c_20_out_5, c_20_out_6, c_20_out_7, c_20_out_8,
       c_21_out_5, c_21_out_6, c_21_out_7, c_21_out_8, c_22_out_5, c_22_out_6, c_22_out_7, c_22_out_8,
       c_23_out_5, c_23_out_6, c_23_out_7, c_23_out_8, c_24_out_5, c_24_out_6, c_24_out_7, c_24_out_8,
       c_25_out_5, c_25_out_6, c_25_out_7, c_25_out_8, c_26_out_5, c_26_out_6, c_26_out_7, c_26_out_8,
       c_27_out_5, c_27_out_6, c_27_out_7, c_27_out_8, c_28_out_5, c_28_out_6, c_28_out_7, c_28_out_8,
       c_29_out_5, c_29_out_6, c_29_out_7, c_29_out_8, c_30_out_5, c_30_out_6, c_30_out_7, c_30_out_8,
       c_31_out_5, c_31_out_6, c_31_out_7, c_31_out_8, c_32_out_5, c_32_out_6, c_32_out_7, c_32_out_8,
       c_33_out_5, c_33_out_6, c_33_out_7, c_33_out_8, c_34_out_5, c_34_out_6, c_34_out_7, c_34_out_8,
       c_35_out_5, c_35_out_6, c_35_out_7, c_35_out_8, c_36_out_5, c_36_out_6, c_36_out_7, c_36_out_8,
       c_37_out_5, c_37_out_6, c_37_out_7, c_37_out_8, c_38_out_5, c_38_out_6, c_38_out_7, c_38_out_8,
       c_39_out_5, c_39_out_6, c_39_out_7, c_39_out_8, c_40_out_5, c_40_out_6, c_40_out_7, c_40_out_8,
       c_41_out_5, c_41_out_6, c_41_out_7, c_41_out_8, c_42_out_5, c_42_out_6, c_42_out_7, c_42_out_8,
       c_43_out_5, c_43_out_6, c_43_out_7, c_43_out_8, c_44_out_5, c_44_out_6, c_44_out_7, c_44_out_8,
       c_45_out_5, c_45_out_6, c_45_out_7, c_45_out_8, c_46_out_5, c_46_out_6, c_46_out_7, c_46_out_8,
       c_47_out_5, c_47_out_6, c_47_out_7, c_47_out_8, c_48_out_5, c_48_out_6, c_48_out_7, c_48_out_8,
       c_49_out_5, c_49_out_6, c_49_out_7, c_49_out_8, c_50_out_5, c_50_out_6, c_50_out_7, c_50_out_8,
       c_51_out_5, c_51_out_6, c_51_out_7, c_51_out_8, c_52_out_5, c_52_out_6, c_52_out_7, c_52_out_8,
       c_53_out_5, c_53_out_6, c_53_out_7, c_53_out_8, c_54_out_5, c_54_out_6, c_54_out_7, c_54_out_8,
       c_55_out_5, c_55_out_6, c_55_out_7, c_55_out_8, c_58_out_5, c_58_out_6, c_58_out_7, c_58_out_8,
       c_59_out_5, c_59_out_6, c_59_out_7, c_59_out_8, c_60_out_5, c_60_out_6, c_60_out_7, c_60_out_8,
       c_61_out_5, c_61_out_6, c_61_out_7, c_61_out_8, c_62_out_5, c_62_out_6, c_62_out_7, c_62_out_8,
       c_63_out_5, c_63_out_6, c_63_out_7, c_63_out_8, c_64_out_5, c_64_out_6, c_64_out_7, c_64_out_8,
       c_65_out_5, c_65_out_6, c_65_out_7, c_65_out_8, c_66_out_5, c_66_out_6, c_66_out_7, c_66_out_8,
       c_67_out_5, c_67_out_6, c_67_out_7, c_67_out_8, c_68_out_5, c_68_out_6, c_68_out_7, c_68_out_8,
       c_69_out_5, c_69_out_6, c_69_out_7, c_69_out_8, c_70_out_5, c_70_out_6, c_70_out_7, c_70_out_8,
       c_71_out_5, c_71_out_6, c_71_out_7, c_71_out_8, c_72_out_5, c_72_out_6, c_72_out_7, c_72_out_8,
       c_73_out_5, c_73_out_6, c_73_out_7, c_73_out_8, c_74_out_5, c_74_out_6, c_74_out_7, c_74_out_8,
       c_75_out_5, c_75_out_6, c_75_out_7, c_75_out_8, c_76_out_5, c_76_out_6, c_76_out_7, c_76_out_8,
       c_77_out_5, c_77_out_6, c_77_out_7, c_77_out_8, c_78_out_5, c_78_out_6, c_78_out_7, c_78_out_8,
       c_79_out_5, c_79_out_6, c_79_out_7, c_79_out_8, c_80_out_5, c_80_out_6, c_80_out_7, c_80_out_8,
       c_81_out_5, c_81_out_6, c_81_out_7, c_81_out_8, c_82_out_5, c_82_out_6, c_82_out_7, c_82_out_8,
       c_83_out_5, c_83_out_6, c_83_out_7, c_83_out_8, c_84_out_5, c_84_out_6, c_84_out_7, c_84_out_8,
       c_85_out_5, c_85_out_6, c_85_out_7, c_85_out_8, c_86_out_5, c_86_out_6, c_86_out_7, c_86_out_8,
       c_87_out_5, c_87_out_6, c_87_out_7, c_87_out_8, c_88_out_5, c_88_out_6, c_88_out_7, c_88_out_8,
       c_89_out_5, c_89_out_6, c_89_out_7, c_89_out_8, c_90_out_5, c_90_out_6, c_90_out_7, c_90_out_8,
       c_91_out_5, c_91_out_6, c_91_out_7, c_91_out_8, c_92_out_5, c_92_out_6, c_92_out_7, c_92_out_8,
       c_93_out_5, c_93_out_6, c_93_out_7, c_93_out_8, c_94_out_5, c_94_out_6, c_94_out_7, c_94_out_8,
       c_95_out_5, c_95_out_6, c_95_out_7, c_95_out_8, c_96_out_5, c_96_out_6, c_96_out_7, c_96_out_8,
       c_97_out_5, c_97_out_6, c_97_out_7, c_97_out_8, c_98_out_5, c_98_out_6, c_98_out_7, c_98_out_8,
       c_99_out_5, c_99_out_6, c_99_out_7, c_99_out_8, c_100_out_5, c_100_out_6, c_100_out_7, c_100_out_8,
       c_101_out_5, c_101_out_6, c_101_out_7, c_101_out_8, c_102_out_5, c_102_out_6, c_102_out_7,
       c_102_out_8, c_103_out_5, c_103_out_6, c_103_out_7, c_103_out_8, c_106_out_5, c_106_out_6,
       c_106_out_7, c_106_out_8, c_107_out_5, c_107_out_6, c_107_out_7, c_107_out_8, c_108_out_5,
       c_108_out_6, c_108_out_7, c_108_out_8, c_109_out_5, c_109_out_6, c_109_out_7, c_109_out_8,
       c_110_out_5, c_110_out_6, c_110_out_7, c_110_out_8, c_111_out_5, c_111_out_6, c_111_out_7,
       c_111_out_8, c_112_out_5, c_112_out_6, c_112_out_7, c_112_out_8, c_113_out_5, c_113_out_6,
       c_113_out_7, c_113_out_8, c_114_out_5, c_114_out_6, c_114_out_7, c_114_out_8, c_115_out_5,
       c_115_out_6, c_115_out_7, c_115_out_8, c_116_out_5, c_116_out_6, c_116_out_7, c_116_out_8,
       c_117_out_5, c_117_out_6, c_117_out_7, c_117_out_8, c_118_out_5, c_118_out_6, c_118_out_7,
       c_118_out_8, c_119_out_5, c_119_out_6, c_119_out_7, c_119_out_8, c_120_out_5, c_120_out_6,
       c_120_out_7, c_120_out_8, c_121_out_5, c_121_out_6, c_121_out_7, c_121_out_8, c_122_out_5,
       c_122_out_6, c_122_out_7, c_122_out_8, c_123_out_5, c_123_out_6, c_123_out_7, c_123_out_8,
       c_124_out_5, c_124_out_6, c_124_out_7, c_124_out_8, c_125_out_5, c_125_out_6, c_125_out_7,
       c_125_out_8, c_126_out_5, c_126_out_6, c_126_out_7, c_126_out_8, c_127_out_5, c_127_out_6,
       c_127_out_7, c_127_out_8, c_128_out_5, c_128_out_6, c_128_out_7, c_128_out_8, c_129_out_5,
       c_129_out_6, c_129_out_7, c_129_out_8, c_130_out_5, c_130_out_6, c_130_out_7, c_130_out_8,
       c_131_out_5, c_131_out_6, c_131_out_7, c_131_out_8, c_132_out_5, c_132_out_6, c_132_out_7,
       c_132_out_8, c_133_out_5, c_133_out_6, c_133_out_7, c_133_out_8, c_134_out_5, c_134_out_6,
       c_134_out_7, c_134_out_8, c_135_out_5, c_135_out_6, c_135_out_7, c_135_out_8, c_138_out_5,
       c_138_out_6, c_138_out_7, c_138_out_8, c_139_out_5, c_139_out_6, c_139_out_7, c_139_out_8,
       c_140_out_5, c_140_out_6, c_140_out_7, c_140_out_8, c_141_out_5, c_141_out_6, c_141_out_7,
       c_141_out_8, c_142_out_5, c_142_out_6, c_142_out_7, c_142_out_8, c_143_out_5, c_143_out_6,
       c_143_out_7, c_143_out_8, c_144_out_5, c_144_out_6, c_144_out_7, c_144_out_8, c_145_out_5,
       c_145_out_6, c_145_out_7, c_145_out_8, c_146_out_5, c_146_out_6, c_146_out_7, c_146_out_8,
       c_147_out_5, c_147_out_6, c_147_out_7, c_147_out_8, c_148_out_5, c_148_out_6, c_148_out_7,
       c_148_out_8, c_149_out_5, c_149_out_6, c_149_out_7, c_149_out_8, c_150_out_5, c_150_out_6,
       c_150_out_7, c_150_out_8, c_151_out_5, c_151_out_6, c_151_out_7, c_151_out_8, c_154_out_5,
       c_154_out_6, c_154_out_7, c_154_out_8;

  c c_1 (
    .in_1(1'b0), .in_2(c_30_out_5), .in_3(c_33_out_5), .in_4(c_35_out_5), .out_5(c_1_out_5),
    .out_6(c_1_out_6), .out_7(c_1_out_7), .out_8(c_1_out_8));
  c c_2 (
    .in_1(1'b0), .in_2(c_1_out_5), .in_3(c_38_out_5), .in_4(c_40_out_5), .out_5(c_2_out_5),
    .out_6(c_2_out_6), .out_7(c_2_out_7), .out_8(c_2_out_8));
  c c_3 (
    .in_1(c_2_out_6), .in_2(c_2_out_7), .in_3(c_2_out_8), .in_4(c_43_out_5), .out_5(c_3_out_5),
    .out_6(c_3_out_6), .out_7(c_3_out_7), .out_8(c_3_out_8));
  c c_4 (
    .in_1(1'b0), .in_2(c_2_out_5), .in_3(c_3_out_5), .in_4(c_47_out_5), .out_5(c_4_out_5), .out_6(c_4_out_6),
    .out_7(c_4_out_7), .out_8(c_4_out_8));
  c c_5 (
    .in_1(c_4_out_6), .in_2(c_4_out_7), .in_3(c_4_out_8), .in_4(c_49_out_5), .out_5(c_5_out_5),
    .out_6(c_5_out_6), .out_7(c_5_out_7), .out_8(c_5_out_8));
  c c_6 (
    .in_1(c_5_out_6), .in_2(c_5_out_7), .in_3(c_5_out_8), .in_4(c_50_out_5), .out_5(c_6_out_5),
    .out_6(c_6_out_6), .out_7(c_6_out_7), .out_8(c_6_out_8));
  c c_7 (
    .in_1(1'b0), .in_2(c_4_out_5), .in_3(c_5_out_5), .in_4(c_6_out_5), .out_6(c_7_out_6), .out_7(c_7_out_7),
    .out_8(c_7_out_8));  // open: out_5
  c c_8 (
    .in_1(c_7_out_6), .in_2(c_7_out_7), .in_3(c_7_out_8), .in_4(c_55_out_5), .out_6(out_2[3]),
    .out_7(out_2[2]), .out_8(out_2[1]));  // open: out_5
  c c_9 (
    .in_1(1'b0), .in_2(in_1[31]), .in_3(in_1[30]), .in_4(in_1[29]), .out_5(c_9_out_5), .out_6(c_9_out_6),
    .out_7(c_9_out_7), .out_8(c_9_out_8));
  c c_10 (
    .in_1(c_9_out_6), .in_2(c_9_out_7), .in_3(c_9_out_8), .in_4(in_1[28]), .out_5(c_10_out_5),
    .out_6(c_10_out_6), .out_7(c_10_out_7), .out_8(c_10_out_8));
  c c_11 (
    .in_1(c_10_out_6), .in_2(c_10_out_7), .in_3(c_10_out_8), .in_4(in_1[27]), .out_5(c_11_out_5),
    .out_6(c_11_out_6), .out_7(c_11_out_7), .out_8(c_11_out_8));
  c c_12 (
    .in_1(1'b0), .in_2(c_9_out_5), .in_3(c_10_out_5), .in_4(c_11_out_5), .out_5(c_12_out_5),
    .out_6(c_12_out_6), .out_7(c_12_out_7), .out_8(c_12_out_8));
  c c_13 (
    .in_1(c_12_out_6), .in_2(c_12_out_7), .in_3(c_12_out_8), .in_4(c_58_out_5), .out_5(c_13_out_5),
    .out_6(c_13_out_6), .out_7(c_13_out_7), .out_8(c_13_out_8));
  c c_14 (
    .in_1(c_13_out_6), .in_2(c_13_out_7), .in_3(c_13_out_8), .in_4(c_59_out_5), .out_5(c_14_out_5),
    .out_6(c_14_out_6), .out_7(c_14_out_7), .out_8(c_14_out_8));
  c c_15 (
    .in_1(1'b0), .in_2(c_12_out_5), .in_3(c_13_out_5), .in_4(c_14_out_5), .out_5(c_15_out_5),
    .out_6(c_15_out_6), .out_7(c_15_out_7), .out_8(c_15_out_8));
  c c_16 (
    .in_1(c_14_out_6), .in_2(c_14_out_7), .in_3(c_14_out_8), .in_4(c_60_out_5), .out_5(c_16_out_5),
    .out_6(c_16_out_6), .out_7(c_16_out_7), .out_8(c_16_out_8));
  c c_17 (
    .in_1(c_15_out_6), .in_2(c_15_out_7), .in_3(c_15_out_8), .in_4(c_16_out_5), .out_5(c_17_out_5),
    .out_6(c_17_out_6), .out_7(c_17_out_7), .out_8(c_17_out_8));
  c c_18 (
    .in_1(c_17_out_6), .in_2(c_17_out_7), .in_3(c_17_out_8), .in_4(c_63_out_5), .out_5(c_18_out_5),
    .out_6(c_18_out_6), .out_7(c_18_out_7), .out_8(c_18_out_8));
  c c_19 (
    .in_1(1'b0), .in_2(c_15_out_5), .in_3(c_17_out_5), .in_4(c_18_out_5), .out_5(c_19_out_5),
    .out_6(c_19_out_6), .out_7(c_19_out_7), .out_8(c_19_out_8));
  c c_20 (
    .in_1(c_18_out_6), .in_2(c_18_out_7), .in_3(c_18_out_8), .in_4(c_64_out_5), .out_5(c_20_out_5),
    .out_6(c_20_out_6), .out_7(c_20_out_7), .out_8(c_20_out_8));
  c c_21 (
    .in_1(c_19_out_6), .in_2(c_19_out_7), .in_3(c_19_out_8), .in_4(c_20_out_5), .out_5(c_21_out_5),
    .out_6(c_21_out_6), .out_7(c_21_out_7), .out_8(c_21_out_8));
  c c_22 (
    .in_1(c_20_out_6), .in_2(c_20_out_7), .in_3(c_20_out_8), .in_4(c_66_out_5), .out_5(c_22_out_5),
    .out_6(c_22_out_6), .out_7(c_22_out_7), .out_8(c_22_out_8));
  c c_23 (
    .in_1(c_21_out_6), .in_2(c_21_out_7), .in_3(c_21_out_8), .in_4(c_22_out_5), .out_5(c_23_out_5),
    .out_6(c_23_out_6), .out_7(c_23_out_7), .out_8(c_23_out_8));
  c c_24 (
    .in_1(1'b0), .in_2(c_19_out_5), .in_3(c_21_out_5), .in_4(c_23_out_5), .out_5(c_24_out_5),
    .out_6(c_24_out_6), .out_7(c_24_out_7), .out_8(c_24_out_8));
  c c_25 (
    .in_1(c_23_out_6), .in_2(c_23_out_7), .in_3(c_23_out_8), .in_4(c_70_out_5), .out_5(c_25_out_5),
    .out_6(c_25_out_6), .out_7(c_25_out_7), .out_8(c_25_out_8));
  c c_26 (
    .in_1(c_24_out_6), .in_2(c_24_out_7), .in_3(c_24_out_8), .in_4(c_25_out_5), .out_5(c_26_out_5),
    .out_6(c_26_out_6), .out_7(c_26_out_7), .out_8(c_26_out_8));
  c c_27 (
    .in_1(c_25_out_6), .in_2(c_25_out_7), .in_3(c_25_out_8), .in_4(c_73_out_5), .out_5(c_27_out_5),
    .out_6(c_27_out_6), .out_7(c_27_out_7), .out_8(c_27_out_8));
  c c_28 (
    .in_1(c_27_out_6), .in_2(c_27_out_7), .in_3(c_27_out_8), .in_4(c_74_out_5), .out_5(c_28_out_5),
    .out_6(c_28_out_6), .out_7(c_28_out_7), .out_8(c_28_out_8));
  c c_29 (
    .in_1(c_26_out_6), .in_2(c_26_out_7), .in_3(c_26_out_8), .in_4(c_27_out_5), .out_5(c_29_out_5),
    .out_6(c_29_out_6), .out_7(c_29_out_7), .out_8(c_29_out_8));
  c c_30 (
    .in_1(1'b0), .in_2(c_24_out_5), .in_3(c_26_out_5), .in_4(c_29_out_5), .out_5(c_30_out_5),
    .out_6(c_30_out_6), .out_7(c_30_out_7), .out_8(c_30_out_8));
  c c_31 (
    .in_1(c_29_out_6), .in_2(c_29_out_7), .in_3(c_29_out_8), .in_4(c_28_out_5), .out_5(c_31_out_5),
    .out_6(c_31_out_6), .out_7(c_31_out_7), .out_8(c_31_out_8));
  c c_32 (
    .in_1(c_31_out_6), .in_2(c_31_out_7), .in_3(c_31_out_8), .in_4(c_78_out_5), .out_5(c_32_out_5),
    .out_6(c_32_out_6), .out_7(c_32_out_7), .out_8(c_32_out_8));
  c c_33 (
    .in_1(c_30_out_6), .in_2(c_30_out_7), .in_3(c_30_out_8), .in_4(c_31_out_5), .out_5(c_33_out_5),
    .out_6(c_33_out_6), .out_7(c_33_out_7), .out_8(c_33_out_8));
  c c_34 (
    .in_1(c_32_out_6), .in_2(c_32_out_7), .in_3(c_32_out_8), .in_4(c_80_out_5), .out_5(c_34_out_5),
    .out_6(c_34_out_6), .out_7(c_34_out_7), .out_8(c_34_out_8));
  c c_35 (
    .in_1(c_33_out_6), .in_2(c_33_out_7), .in_3(c_33_out_8), .in_4(c_32_out_5), .out_5(c_35_out_5),
    .out_6(c_35_out_6), .out_7(c_35_out_7), .out_8(c_35_out_8));
  c c_36 (
    .in_1(c_34_out_6), .in_2(c_34_out_7), .in_3(c_34_out_8), .in_4(c_82_out_5), .out_5(c_36_out_5),
    .out_6(c_36_out_6), .out_7(c_36_out_7), .out_8(c_36_out_8));
  c c_37 (
    .in_1(c_35_out_6), .in_2(c_35_out_7), .in_3(c_35_out_8), .in_4(c_34_out_5), .out_5(c_37_out_5),
    .out_6(c_37_out_6), .out_7(c_37_out_7), .out_8(c_37_out_8));
  c c_38 (
    .in_1(c_1_out_6), .in_2(c_1_out_7), .in_3(c_1_out_8), .in_4(c_37_out_5), .out_5(c_38_out_5),
    .out_6(c_38_out_6), .out_7(c_38_out_7), .out_8(c_38_out_8));
  c c_39 (
    .in_1(c_37_out_6), .in_2(c_37_out_7), .in_3(c_37_out_8), .in_4(c_36_out_5), .out_5(c_39_out_5),
    .out_6(c_39_out_6), .out_7(c_39_out_7), .out_8(c_39_out_8));
  c c_40 (
    .in_1(c_38_out_6), .in_2(c_38_out_7), .in_3(c_38_out_8), .in_4(c_39_out_5), .out_5(c_40_out_5),
    .out_6(c_40_out_6), .out_7(c_40_out_7), .out_8(c_40_out_8));
  c c_41 (
    .in_1(c_39_out_6), .in_2(c_39_out_7), .in_3(c_39_out_8), .in_4(c_86_out_5), .out_5(c_41_out_5),
    .out_6(c_41_out_6), .out_7(c_41_out_7), .out_8(c_41_out_8));
  c c_42 (
    .in_1(c_41_out_6), .in_2(c_41_out_7), .in_3(c_41_out_8), .in_4(c_88_out_5), .out_5(c_42_out_5),
    .out_6(c_42_out_6), .out_7(c_42_out_7), .out_8(c_42_out_8));
  c c_43 (
    .in_1(c_40_out_6), .in_2(c_40_out_7), .in_3(c_40_out_8), .in_4(c_41_out_5), .out_5(c_43_out_5),
    .out_6(c_43_out_6), .out_7(c_43_out_7), .out_8(c_43_out_8));
  c c_44 (
    .in_1(c_43_out_6), .in_2(c_43_out_7), .in_3(c_43_out_8), .in_4(c_42_out_5), .out_5(c_44_out_5),
    .out_6(c_44_out_6), .out_7(c_44_out_7), .out_8(c_44_out_8));
  c c_45 (
    .in_1(c_42_out_6), .in_2(c_42_out_7), .in_3(c_42_out_8), .in_4(c_91_out_5), .out_5(c_45_out_5),
    .out_6(c_45_out_6), .out_7(c_45_out_7), .out_8(c_45_out_8));
  c c_46 (
    .in_1(c_44_out_6), .in_2(c_44_out_7), .in_3(c_44_out_8), .in_4(c_45_out_5), .out_5(c_46_out_5),
    .out_6(c_46_out_6), .out_7(c_46_out_7), .out_8(c_46_out_8));
  c c_47 (
    .in_1(c_3_out_6), .in_2(c_3_out_7), .in_3(c_3_out_8), .in_4(c_44_out_5), .out_5(c_47_out_5),
    .out_6(c_47_out_6), .out_7(c_47_out_7), .out_8(c_47_out_8));
  c c_48 (
    .in_1(c_46_out_6), .in_2(c_46_out_7), .in_3(c_46_out_8), .in_4(c_94_out_5), .out_5(c_48_out_5),
    .out_6(c_48_out_6), .out_7(c_48_out_7), .out_8(c_48_out_8));
  c c_49 (
    .in_1(c_47_out_6), .in_2(c_47_out_7), .in_3(c_47_out_8), .in_4(c_46_out_5), .out_5(c_49_out_5),
    .out_6(c_49_out_6), .out_7(c_49_out_7), .out_8(c_49_out_8));
  c c_50 (
    .in_1(c_49_out_6), .in_2(c_49_out_7), .in_3(c_49_out_8), .in_4(c_48_out_5), .out_5(c_50_out_5),
    .out_6(c_50_out_6), .out_7(c_50_out_7), .out_8(c_50_out_8));
  c c_51 (
    .in_1(c_48_out_6), .in_2(c_48_out_7), .in_3(c_48_out_8), .in_4(c_97_out_5), .out_5(c_51_out_5),
    .out_6(c_51_out_6), .out_7(c_51_out_7), .out_8(c_51_out_8));
  c c_52 (
    .in_1(c_50_out_6), .in_2(c_50_out_7), .in_3(c_50_out_8), .in_4(c_51_out_5), .out_5(c_52_out_5),
    .out_6(c_52_out_6), .out_7(c_52_out_7), .out_8(c_52_out_8));
  c c_53 (
    .in_1(c_51_out_6), .in_2(c_51_out_7), .in_3(c_51_out_8), .in_4(c_98_out_5), .out_5(c_53_out_5),
    .out_6(c_53_out_6), .out_7(c_53_out_7), .out_8(c_53_out_8));
  c c_54 (
    .in_1(c_52_out_6), .in_2(c_52_out_7), .in_3(c_52_out_8), .in_4(c_53_out_5), .out_5(c_54_out_5),
    .out_6(c_54_out_6), .out_7(c_54_out_7), .out_8(c_54_out_8));
  c c_55 (
    .in_1(c_6_out_6), .in_2(c_6_out_7), .in_3(c_6_out_8), .in_4(c_52_out_5), .out_5(c_55_out_5),
    .out_6(c_55_out_6), .out_7(c_55_out_7), .out_8(c_55_out_8));
  c c_56 (
    .in_1(c_54_out_6), .in_2(c_54_out_7), .in_3(c_54_out_8), .in_4(c_102_out_5), .out_5(out_3[0]),
    .out_6(out_4[3]), .out_7(out_4[2]), .out_8(out_4[1]));
  c c_57 (
    .in_1(c_55_out_6), .in_2(c_55_out_7), .in_3(c_55_out_8), .in_4(c_54_out_5), .out_5(out_2[0]),
    .out_6(out_3[3]), .out_7(out_3[2]), .out_8(out_3[1]));
  c c_58 (
    .in_1(c_11_out_6), .in_2(c_11_out_7), .in_3(c_11_out_8), .in_4(in_1[26]), .out_5(c_58_out_5),
    .out_6(c_58_out_6), .out_7(c_58_out_7), .out_8(c_58_out_8));
  c c_59 (
    .in_1(c_58_out_6), .in_2(c_58_out_7), .in_3(c_58_out_8), .in_4(in_1[25]), .out_5(c_59_out_5),
    .out_6(c_59_out_6), .out_7(c_59_out_7), .out_8(c_59_out_8));
  c c_60 (
    .in_1(c_59_out_6), .in_2(c_59_out_7), .in_3(c_59_out_8), .in_4(in_1[24]), .out_5(c_60_out_5),
    .out_6(c_60_out_6), .out_7(c_60_out_7), .out_8(c_60_out_8));
  c c_61 (
    .in_1(c_60_out_6), .in_2(c_60_out_7), .in_3(c_60_out_8), .in_4(in_1[23]), .out_5(c_61_out_5),
    .out_6(c_61_out_6), .out_7(c_61_out_7), .out_8(c_61_out_8));
  c c_62 (
    .in_1(c_61_out_6), .in_2(c_61_out_7), .in_3(c_61_out_8), .in_4(in_1[22]), .out_5(c_62_out_5),
    .out_6(c_62_out_6), .out_7(c_62_out_7), .out_8(c_62_out_8));
  c c_63 (
    .in_1(c_16_out_6), .in_2(c_16_out_7), .in_3(c_16_out_8), .in_4(c_61_out_5), .out_5(c_63_out_5),
    .out_6(c_63_out_6), .out_7(c_63_out_7), .out_8(c_63_out_8));
  c c_64 (
    .in_1(c_63_out_6), .in_2(c_63_out_7), .in_3(c_63_out_8), .in_4(c_62_out_5), .out_5(c_64_out_5),
    .out_6(c_64_out_6), .out_7(c_64_out_7), .out_8(c_64_out_8));
  c c_65 (
    .in_1(c_62_out_6), .in_2(c_62_out_7), .in_3(c_62_out_8), .in_4(in_1[21]), .out_5(c_65_out_5),
    .out_6(c_65_out_6), .out_7(c_65_out_7), .out_8(c_65_out_8));
  c c_66 (
    .in_1(c_64_out_6), .in_2(c_64_out_7), .in_3(c_64_out_8), .in_4(c_65_out_5), .out_5(c_66_out_5),
    .out_6(c_66_out_6), .out_7(c_66_out_7), .out_8(c_66_out_8));
  c c_67 (
    .in_1(c_65_out_6), .in_2(c_65_out_7), .in_3(c_65_out_8), .in_4(in_1[20]), .out_5(c_67_out_5),
    .out_6(c_67_out_6), .out_7(c_67_out_7), .out_8(c_67_out_8));
  c c_68 (
    .in_1(c_67_out_6), .in_2(c_67_out_7), .in_3(c_67_out_8), .in_4(in_1[19]), .out_5(c_68_out_5),
    .out_6(c_68_out_6), .out_7(c_68_out_7), .out_8(c_68_out_8));
  c c_69 (
    .in_1(c_66_out_6), .in_2(c_66_out_7), .in_3(c_66_out_8), .in_4(c_67_out_5), .out_5(c_69_out_5),
    .out_6(c_69_out_6), .out_7(c_69_out_7), .out_8(c_69_out_8));
  c c_70 (
    .in_1(c_22_out_6), .in_2(c_22_out_7), .in_3(c_22_out_8), .in_4(c_69_out_5), .out_5(c_70_out_5),
    .out_6(c_70_out_6), .out_7(c_70_out_7), .out_8(c_70_out_8));
  c c_71 (
    .in_1(c_69_out_6), .in_2(c_69_out_7), .in_3(c_69_out_8), .in_4(c_68_out_5), .out_5(c_71_out_5),
    .out_6(c_71_out_6), .out_7(c_71_out_7), .out_8(c_71_out_8));
  c c_72 (
    .in_1(c_71_out_6), .in_2(c_71_out_7), .in_3(c_71_out_8), .in_4(c_106_out_5), .out_5(c_72_out_5),
    .out_6(c_72_out_6), .out_7(c_72_out_7), .out_8(c_72_out_8));
  c c_73 (
    .in_1(c_70_out_6), .in_2(c_70_out_7), .in_3(c_70_out_8), .in_4(c_71_out_5), .out_5(c_73_out_5),
    .out_6(c_73_out_6), .out_7(c_73_out_7), .out_8(c_73_out_8));
  c c_74 (
    .in_1(c_73_out_6), .in_2(c_73_out_7), .in_3(c_73_out_8), .in_4(c_72_out_5), .out_5(c_74_out_5),
    .out_6(c_74_out_6), .out_7(c_74_out_7), .out_8(c_74_out_8));
  c c_75 (
    .in_1(c_72_out_6), .in_2(c_72_out_7), .in_3(c_72_out_8), .in_4(c_107_out_5), .out_5(c_75_out_5),
    .out_6(c_75_out_6), .out_7(c_75_out_7), .out_8(c_75_out_8));
  c c_76 (
    .in_1(c_75_out_6), .in_2(c_75_out_7), .in_3(c_75_out_8), .in_4(c_108_out_5), .out_5(c_76_out_5),
    .out_6(c_76_out_6), .out_7(c_76_out_7), .out_8(c_76_out_8));
  c c_77 (
    .in_1(c_74_out_6), .in_2(c_74_out_7), .in_3(c_74_out_8), .in_4(c_75_out_5), .out_5(c_77_out_5),
    .out_6(c_77_out_6), .out_7(c_77_out_7), .out_8(c_77_out_8));
  c c_78 (
    .in_1(c_28_out_6), .in_2(c_28_out_7), .in_3(c_28_out_8), .in_4(c_77_out_5), .out_5(c_78_out_5),
    .out_6(c_78_out_6), .out_7(c_78_out_7), .out_8(c_78_out_8));
  c c_79 (
    .in_1(c_77_out_6), .in_2(c_77_out_7), .in_3(c_77_out_8), .in_4(c_76_out_5), .out_5(c_79_out_5),
    .out_6(c_79_out_6), .out_7(c_79_out_7), .out_8(c_79_out_8));
  c c_80 (
    .in_1(c_78_out_6), .in_2(c_78_out_7), .in_3(c_78_out_8), .in_4(c_79_out_5), .out_5(c_80_out_5),
    .out_6(c_80_out_6), .out_7(c_80_out_7), .out_8(c_80_out_8));
  c c_81 (
    .in_1(c_79_out_6), .in_2(c_79_out_7), .in_3(c_79_out_8), .in_4(c_110_out_5), .out_5(c_81_out_5),
    .out_6(c_81_out_6), .out_7(c_81_out_7), .out_8(c_81_out_8));
  c c_82 (
    .in_1(c_80_out_6), .in_2(c_80_out_7), .in_3(c_80_out_8), .in_4(c_81_out_5), .out_5(c_82_out_5),
    .out_6(c_82_out_6), .out_7(c_82_out_7), .out_8(c_82_out_8));
  c c_83 (
    .in_1(c_81_out_6), .in_2(c_81_out_7), .in_3(c_81_out_8), .in_4(c_113_out_5), .out_5(c_83_out_5),
    .out_6(c_83_out_6), .out_7(c_83_out_7), .out_8(c_83_out_8));
  c c_84 (
    .in_1(c_83_out_6), .in_2(c_83_out_7), .in_3(c_83_out_8), .in_4(c_114_out_5), .out_5(c_84_out_5),
    .out_6(c_84_out_6), .out_7(c_84_out_7), .out_8(c_84_out_8));
  c c_85 (
    .in_1(c_82_out_6), .in_2(c_82_out_7), .in_3(c_82_out_8), .in_4(c_83_out_5), .out_5(c_85_out_5),
    .out_6(c_85_out_6), .out_7(c_85_out_7), .out_8(c_85_out_8));
  c c_86 (
    .in_1(c_36_out_6), .in_2(c_36_out_7), .in_3(c_36_out_8), .in_4(c_85_out_5), .out_5(c_86_out_5),
    .out_6(c_86_out_6), .out_7(c_86_out_7), .out_8(c_86_out_8));
  c c_87 (
    .in_1(c_85_out_6), .in_2(c_85_out_7), .in_3(c_85_out_8), .in_4(c_84_out_5), .out_5(c_87_out_5),
    .out_6(c_87_out_6), .out_7(c_87_out_7), .out_8(c_87_out_8));
  c c_88 (
    .in_1(c_86_out_6), .in_2(c_86_out_7), .in_3(c_86_out_8), .in_4(c_87_out_5), .out_5(c_88_out_5),
    .out_6(c_88_out_6), .out_7(c_88_out_7), .out_8(c_88_out_8));
  c c_89 (
    .in_1(c_87_out_6), .in_2(c_87_out_7), .in_3(c_87_out_8), .in_4(c_119_out_5), .out_5(c_89_out_5),
    .out_6(c_89_out_6), .out_7(c_89_out_7), .out_8(c_89_out_8));
  c c_90 (
    .in_1(c_89_out_6), .in_2(c_89_out_7), .in_3(c_89_out_8), .in_4(c_121_out_5), .out_5(c_90_out_5),
    .out_6(c_90_out_6), .out_7(c_90_out_7), .out_8(c_90_out_8));
  c c_91 (
    .in_1(c_88_out_6), .in_2(c_88_out_7), .in_3(c_88_out_8), .in_4(c_89_out_5), .out_5(c_91_out_5),
    .out_6(c_91_out_6), .out_7(c_91_out_7), .out_8(c_91_out_8));
  c c_92 (
    .in_1(c_91_out_6), .in_2(c_91_out_7), .in_3(c_91_out_8), .in_4(c_90_out_5), .out_5(c_92_out_5),
    .out_6(c_92_out_6), .out_7(c_92_out_7), .out_8(c_92_out_8));
  c c_93 (
    .in_1(c_90_out_6), .in_2(c_90_out_7), .in_3(c_90_out_8), .in_4(c_122_out_5), .out_5(c_93_out_5),
    .out_6(c_93_out_6), .out_7(c_93_out_7), .out_8(c_93_out_8));
  c c_94 (
    .in_1(c_45_out_6), .in_2(c_45_out_7), .in_3(c_45_out_8), .in_4(c_92_out_5), .out_5(c_94_out_5),
    .out_6(c_94_out_6), .out_7(c_94_out_7), .out_8(c_94_out_8));
  c c_95 (
    .in_1(c_92_out_6), .in_2(c_92_out_7), .in_3(c_92_out_8), .in_4(c_93_out_5), .out_5(c_95_out_5),
    .out_6(c_95_out_6), .out_7(c_95_out_7), .out_8(c_95_out_8));
  c c_96 (
    .in_1(c_95_out_6), .in_2(c_95_out_7), .in_3(c_95_out_8), .in_4(c_126_out_5), .out_5(c_96_out_5),
    .out_6(c_96_out_6), .out_7(c_96_out_7), .out_8(c_96_out_8));
  c c_97 (
    .in_1(c_94_out_6), .in_2(c_94_out_7), .in_3(c_94_out_8), .in_4(c_95_out_5), .out_5(c_97_out_5),
    .out_6(c_97_out_6), .out_7(c_97_out_7), .out_8(c_97_out_8));
  c c_98 (
    .in_1(c_97_out_6), .in_2(c_97_out_7), .in_3(c_97_out_8), .in_4(c_96_out_5), .out_5(c_98_out_5),
    .out_6(c_98_out_6), .out_7(c_98_out_7), .out_8(c_98_out_8));
  c c_99 (
    .in_1(c_96_out_6), .in_2(c_96_out_7), .in_3(c_96_out_8), .in_4(c_128_out_5), .out_5(c_99_out_5),
    .out_6(c_99_out_6), .out_7(c_99_out_7), .out_8(c_99_out_8));
  c c_100 (
    .in_1(c_98_out_6), .in_2(c_98_out_7), .in_3(c_98_out_8), .in_4(c_99_out_5), .out_5(c_100_out_5),
    .out_6(c_100_out_6), .out_7(c_100_out_7), .out_8(c_100_out_8));
  c c_101 (
    .in_1(c_99_out_6), .in_2(c_99_out_7), .in_3(c_99_out_8), .in_4(c_131_out_5), .out_5(c_101_out_5),
    .out_6(c_101_out_6), .out_7(c_101_out_7), .out_8(c_101_out_8));
  c c_102 (
    .in_1(c_53_out_6), .in_2(c_53_out_7), .in_3(c_53_out_8), .in_4(c_100_out_5), .out_5(c_102_out_5),
    .out_6(c_102_out_6), .out_7(c_102_out_7), .out_8(c_102_out_8));
  c c_103 (
    .in_1(c_100_out_6), .in_2(c_100_out_7), .in_3(c_100_out_8), .in_4(c_101_out_5), .out_5(c_103_out_5),
    .out_6(c_103_out_6), .out_7(c_103_out_7), .out_8(c_103_out_8));
  c c_104 (
    .in_1(c_103_out_6), .in_2(c_103_out_7), .in_3(c_103_out_8), .in_4(c_135_out_5), .out_5(out_5[0]),
    .out_6(out_6[3]), .out_7(out_6[2]), .out_8(out_6[1]));
  c c_105 (
    .in_1(c_102_out_6), .in_2(c_102_out_7), .in_3(c_102_out_8), .in_4(c_103_out_5), .out_5(out_4[0]),
    .out_6(out_5[3]), .out_7(out_5[2]), .out_8(out_5[1]));
  c c_106 (
    .in_1(c_68_out_6), .in_2(c_68_out_7), .in_3(c_68_out_8), .in_4(in_1[18]), .out_5(c_106_out_5),
    .out_6(c_106_out_6), .out_7(c_106_out_7), .out_8(c_106_out_8));
  c c_107 (
    .in_1(c_106_out_6), .in_2(c_106_out_7), .in_3(c_106_out_8), .in_4(in_1[17]), .out_5(c_107_out_5),
    .out_6(c_107_out_6), .out_7(c_107_out_7), .out_8(c_107_out_8));
  c c_108 (
    .in_1(c_107_out_6), .in_2(c_107_out_7), .in_3(c_107_out_8), .in_4(in_1[16]), .out_5(c_108_out_5),
    .out_6(c_108_out_6), .out_7(c_108_out_7), .out_8(c_108_out_8));
  c c_109 (
    .in_1(c_108_out_6), .in_2(c_108_out_7), .in_3(c_108_out_8), .in_4(in_1[15]), .out_5(c_109_out_5),
    .out_6(c_109_out_6), .out_7(c_109_out_7), .out_8(c_109_out_8));
  c c_110 (
    .in_1(c_76_out_6), .in_2(c_76_out_7), .in_3(c_76_out_8), .in_4(c_109_out_5), .out_5(c_110_out_5),
    .out_6(c_110_out_6), .out_7(c_110_out_7), .out_8(c_110_out_8));
  c c_111 (
    .in_1(c_109_out_6), .in_2(c_109_out_7), .in_3(c_109_out_8), .in_4(in_1[14]), .out_5(c_111_out_5),
    .out_6(c_111_out_6), .out_7(c_111_out_7), .out_8(c_111_out_8));
  c c_112 (
    .in_1(c_111_out_6), .in_2(c_111_out_7), .in_3(c_111_out_8), .in_4(in_1[13]), .out_5(c_112_out_5),
    .out_6(c_112_out_6), .out_7(c_112_out_7), .out_8(c_112_out_8));
  c c_113 (
    .in_1(c_110_out_6), .in_2(c_110_out_7), .in_3(c_110_out_8), .in_4(c_111_out_5), .out_5(c_113_out_5),
    .out_6(c_113_out_6), .out_7(c_113_out_7), .out_8(c_113_out_8));
  c c_114 (
    .in_1(c_113_out_6), .in_2(c_113_out_7), .in_3(c_113_out_8), .in_4(c_112_out_5), .out_5(c_114_out_5),
    .out_6(c_114_out_6), .out_7(c_114_out_7), .out_8(c_114_out_8));
  c c_115 (
    .in_1(c_112_out_6), .in_2(c_112_out_7), .in_3(c_112_out_8), .in_4(in_1[12]), .out_5(c_115_out_5),
    .out_6(c_115_out_6), .out_7(c_115_out_7), .out_8(c_115_out_8));
  c c_116 (
    .in_1(c_114_out_6), .in_2(c_114_out_7), .in_3(c_114_out_8), .in_4(c_115_out_5), .out_5(c_116_out_5),
    .out_6(c_116_out_6), .out_7(c_116_out_7), .out_8(c_116_out_8));
  c c_117 (
    .in_1(c_115_out_6), .in_2(c_115_out_7), .in_3(c_115_out_8), .in_4(in_1[11]), .out_5(c_117_out_5),
    .out_6(c_117_out_6), .out_7(c_117_out_7), .out_8(c_117_out_8));
  c c_118 (
    .in_1(c_116_out_6), .in_2(c_116_out_7), .in_3(c_116_out_8), .in_4(c_117_out_5), .out_5(c_118_out_5),
    .out_6(c_118_out_6), .out_7(c_118_out_7), .out_8(c_118_out_8));
  c c_119 (
    .in_1(c_84_out_6), .in_2(c_84_out_7), .in_3(c_84_out_8), .in_4(c_116_out_5), .out_5(c_119_out_5),
    .out_6(c_119_out_6), .out_7(c_119_out_7), .out_8(c_119_out_8));
  c c_120 (
    .in_1(c_118_out_6), .in_2(c_118_out_7), .in_3(c_118_out_8), .in_4(c_138_out_5), .out_5(c_120_out_5),
    .out_6(c_120_out_6), .out_7(c_120_out_7), .out_8(c_120_out_8));
  c c_121 (
    .in_1(c_119_out_6), .in_2(c_119_out_7), .in_3(c_119_out_8), .in_4(c_118_out_5), .out_5(c_121_out_5),
    .out_6(c_121_out_6), .out_7(c_121_out_7), .out_8(c_121_out_8));
  c c_122 (
    .in_1(c_121_out_6), .in_2(c_121_out_7), .in_3(c_121_out_8), .in_4(c_120_out_5), .out_5(c_122_out_5),
    .out_6(c_122_out_6), .out_7(c_122_out_7), .out_8(c_122_out_8));
  c c_123 (
    .in_1(c_120_out_6), .in_2(c_120_out_7), .in_3(c_120_out_8), .in_4(c_139_out_5), .out_5(c_123_out_5),
    .out_6(c_123_out_6), .out_7(c_123_out_7), .out_8(c_123_out_8));
  c c_124 (
    .in_1(c_122_out_6), .in_2(c_122_out_7), .in_3(c_122_out_8), .in_4(c_123_out_5), .out_5(c_124_out_5),
    .out_6(c_124_out_6), .out_7(c_124_out_7), .out_8(c_124_out_8));
  c c_125 (
    .in_1(c_123_out_6), .in_2(c_123_out_7), .in_3(c_123_out_8), .in_4(c_140_out_5), .out_5(c_125_out_5),
    .out_6(c_125_out_6), .out_7(c_125_out_7), .out_8(c_125_out_8));
  c c_126 (
    .in_1(c_93_out_6), .in_2(c_93_out_7), .in_3(c_93_out_8), .in_4(c_124_out_5), .out_5(c_126_out_5),
    .out_6(c_126_out_6), .out_7(c_126_out_7), .out_8(c_126_out_8));
  c c_127 (
    .in_1(c_124_out_6), .in_2(c_124_out_7), .in_3(c_124_out_8), .in_4(c_125_out_5), .out_5(c_127_out_5),
    .out_6(c_127_out_6), .out_7(c_127_out_7), .out_8(c_127_out_8));
  c c_128 (
    .in_1(c_126_out_6), .in_2(c_126_out_7), .in_3(c_126_out_8), .in_4(c_127_out_5), .out_5(c_128_out_5),
    .out_6(c_128_out_6), .out_7(c_128_out_7), .out_8(c_128_out_8));
  c c_129 (
    .in_1(c_127_out_6), .in_2(c_127_out_7), .in_3(c_127_out_8), .in_4(c_142_out_5), .out_5(c_129_out_5),
    .out_6(c_129_out_6), .out_7(c_129_out_7), .out_8(c_129_out_8));
  c c_130 (
    .in_1(c_129_out_6), .in_2(c_129_out_7), .in_3(c_129_out_8), .in_4(c_144_out_5), .out_5(c_130_out_5),
    .out_6(c_130_out_6), .out_7(c_130_out_7), .out_8(c_130_out_8));
  c c_131 (
    .in_1(c_128_out_6), .in_2(c_128_out_7), .in_3(c_128_out_8), .in_4(c_129_out_5), .out_5(c_131_out_5),
    .out_6(c_131_out_6), .out_7(c_131_out_7), .out_8(c_131_out_8));
  c c_132 (
    .in_1(c_130_out_6), .in_2(c_130_out_7), .in_3(c_130_out_8), .in_4(c_147_out_5), .out_5(c_132_out_5),
    .out_6(c_132_out_6), .out_7(c_132_out_7), .out_8(c_132_out_8));
  c c_133 (
    .in_1(c_131_out_6), .in_2(c_131_out_7), .in_3(c_131_out_8), .in_4(c_130_out_5), .out_5(c_133_out_5),
    .out_6(c_133_out_6), .out_7(c_133_out_7), .out_8(c_133_out_8));
  c c_134 (
    .in_1(c_133_out_6), .in_2(c_133_out_7), .in_3(c_133_out_8), .in_4(c_132_out_5), .out_5(c_134_out_5),
    .out_6(c_134_out_6), .out_7(c_134_out_7), .out_8(c_134_out_8));
  c c_135 (
    .in_1(c_101_out_6), .in_2(c_101_out_7), .in_3(c_101_out_8), .in_4(c_133_out_5), .out_5(c_135_out_5),
    .out_6(c_135_out_6), .out_7(c_135_out_7), .out_8(c_135_out_8));
  c c_136 (
    .in_1(c_134_out_6), .in_2(c_134_out_7), .in_3(c_134_out_8), .in_4(c_151_out_5), .out_5(out_7[0]),
    .out_6(out_8[3]), .out_7(out_8[2]), .out_8(out_8[1]));
  c c_137 (
    .in_1(c_135_out_6), .in_2(c_135_out_7), .in_3(c_135_out_8), .in_4(c_134_out_5), .out_5(out_6[0]),
    .out_6(out_7[3]), .out_7(out_7[2]), .out_8(out_7[1]));
  c c_138 (
    .in_1(c_117_out_6), .in_2(c_117_out_7), .in_3(c_117_out_8), .in_4(in_1[10]), .out_5(c_138_out_5),
    .out_6(c_138_out_6), .out_7(c_138_out_7), .out_8(c_138_out_8));
  c c_139 (
    .in_1(c_138_out_6), .in_2(c_138_out_7), .in_3(c_138_out_8), .in_4(in_1[9]), .out_5(c_139_out_5),
    .out_6(c_139_out_6), .out_7(c_139_out_7), .out_8(c_139_out_8));
  c c_140 (
    .in_1(c_139_out_6), .in_2(c_139_out_7), .in_3(c_139_out_8), .in_4(in_1[8]), .out_5(c_140_out_5),
    .out_6(c_140_out_6), .out_7(c_140_out_7), .out_8(c_140_out_8));
  c c_141 (
    .in_1(c_140_out_6), .in_2(c_140_out_7), .in_3(c_140_out_8), .in_4(in_1[7]), .out_5(c_141_out_5),
    .out_6(c_141_out_6), .out_7(c_141_out_7), .out_8(c_141_out_8));
  c c_142 (
    .in_1(c_125_out_6), .in_2(c_125_out_7), .in_3(c_125_out_8), .in_4(c_141_out_5), .out_5(c_142_out_5),
    .out_6(c_142_out_6), .out_7(c_142_out_7), .out_8(c_142_out_8));
  c c_143 (
    .in_1(c_141_out_6), .in_2(c_141_out_7), .in_3(c_141_out_8), .in_4(in_1[6]), .out_5(c_143_out_5),
    .out_6(c_143_out_6), .out_7(c_143_out_7), .out_8(c_143_out_8));
  c c_144 (
    .in_1(c_142_out_6), .in_2(c_142_out_7), .in_3(c_142_out_8), .in_4(c_143_out_5), .out_5(c_144_out_5),
    .out_6(c_144_out_6), .out_7(c_144_out_7), .out_8(c_144_out_8));
  c c_145 (
    .in_1(c_143_out_6), .in_2(c_143_out_7), .in_3(c_143_out_8), .in_4(in_1[5]), .out_5(c_145_out_5),
    .out_6(c_145_out_6), .out_7(c_145_out_7), .out_8(c_145_out_8));
  c c_146 (
    .in_1(c_145_out_6), .in_2(c_145_out_7), .in_3(c_145_out_8), .in_4(in_1[4]), .out_5(c_146_out_5),
    .out_6(c_146_out_6), .out_7(c_146_out_7), .out_8(c_146_out_8));
  c c_147 (
    .in_1(c_144_out_6), .in_2(c_144_out_7), .in_3(c_144_out_8), .in_4(c_145_out_5), .out_5(c_147_out_5),
    .out_6(c_147_out_6), .out_7(c_147_out_7), .out_8(c_147_out_8));
  c c_148 (
    .in_1(c_147_out_6), .in_2(c_147_out_7), .in_3(c_147_out_8), .in_4(c_146_out_5), .out_5(c_148_out_5),
    .out_6(c_148_out_6), .out_7(c_148_out_7), .out_8(c_148_out_8));
  c c_149 (
    .in_1(c_146_out_6), .in_2(c_146_out_7), .in_3(c_146_out_8), .in_4(in_1[3]), .out_5(c_149_out_5),
    .out_6(c_149_out_6), .out_7(c_149_out_7), .out_8(c_149_out_8));
  c c_150 (
    .in_1(c_148_out_6), .in_2(c_148_out_7), .in_3(c_148_out_8), .in_4(c_149_out_5), .out_5(c_150_out_5),
    .out_6(c_150_out_6), .out_7(c_150_out_7), .out_8(c_150_out_8));
  c c_151 (
    .in_1(c_132_out_6), .in_2(c_132_out_7), .in_3(c_132_out_8), .in_4(c_148_out_5), .out_5(c_151_out_5),
    .out_6(c_151_out_6), .out_7(c_151_out_7), .out_8(c_151_out_8));
  c c_152 (
    .in_1(c_151_out_6), .in_2(c_151_out_7), .in_3(c_151_out_8), .in_4(c_150_out_5), .out_5(out_8[0]),
    .out_6(out_9[3]), .out_7(out_9[2]), .out_8(out_9[1]));
  c c_153 (
    .in_1(c_150_out_6), .in_2(c_150_out_7), .in_3(c_150_out_8), .in_4(c_154_out_5), .out_5(out_9[0]),
    .out_6(out_10[3]), .out_7(out_10[2]), .out_8(out_10[1]));
  c c_154 (
    .in_1(c_149_out_6), .in_2(c_149_out_7), .in_3(c_149_out_8), .in_4(in_1[2]), .out_5(c_154_out_5),
    .out_6(c_154_out_6), .out_7(c_154_out_7), .out_8(c_154_out_8));
  c c_155 (
    .in_1(c_154_out_6), .in_2(c_154_out_7), .in_3(c_154_out_8), .in_4(in_1[1]), .out_5(out_10[0]),
    .out_6(out_11[3]), .out_7(out_11[2]), .out_8(out_11[1]));

  assign out_11[0] = in_1[0];
endmodule

module \斐波那契_Fibonacci_数列计算器  (
  input  [5:0] n,
  input  clear,
  input  clock,
  output [31:0] out_4
);

  wire and_1_out, comparator_1_lt, d_ff_1_q, d_ff_1_qn, \六位移位寄存器_1_out_15 , \六位移位寄存器_1_out_16 ;
  wire [7:0] \八位二进制计数器_1_out_7 ;
  wire [31:0] multiplexer_1_out, multiplexer_2_out, multiplexer_3_out, multiplexer_4_out, multiplexer_5_out,
       multiplexer_6_out, multiplexer_7_out, multiplexer_8_out, register_2_q, register_3_q, register_4_q,
       sqrx_1_a_prime, sqrx_1_b_prime, sqrx_1_c_prime, sqrx_1_d_prime, sqrx_a_1_a_prime_prime,
       sqrx_a_1_b_prime_prime, sqrx_a_1_c_prime_prime, sqrx_a_1_d_prime_prime;

  \八位二进制计数器  \u_八位二进制计数器_1  (
    .in_1({8{1'b0}}), .CPu(clock), .CLR(clear), .nLD(1'b1), .out_7(\八位二进制计数器_1_out_7 ), .en(comparator_1_lt));  // open: Carry
  Comparator #(.mode("unsigned")) comparator_1 (
    .a(\八位二进制计数器_1_out_7 ), .b(8'h6), .lt(comparator_1_lt));  // open: gt, eq
  \六位移位寄存器  \u_六位移位寄存器_1  (
    .clr(1'b0), .LD(clear), .out_16(\六位移位寄存器_1_out_16 ), .clk(clock), .out_15(\六位移位寄存器_1_out_15 ),
    .in_4(n[0]), .in_5(n[1]), .in_6(n[2]), .in_7(n[3]), .in_8(n[4]), .in_9(n[5]));  // open: out_10, out_12, out_13, out_14, out_11
  D_Flip_Flop #(.trigger("high")) d_ff_1 (
    .clk(\六位移位寄存器_1_out_16 ), .D(comparator_1_lt), .Q(d_ff_1_q), .Qn(d_ff_1_qn), .preset(1'b0),
    .en(d_ff_1_qn), .reset(clear));
  and and_1 (and_1_out, comparator_1_lt, clock);
  Multiplexer #(.width(32), .enable("false")) multiplexer_1 (
    .in0(32'h1), .in1(multiplexer_6_out), .out(multiplexer_1_out), .sel(d_ff_1_q));
  Multiplexer #(.width(32), .enable("false")) multiplexer_2 (
    .in0(32'h1), .in1(multiplexer_8_out), .out(multiplexer_2_out), .sel(d_ff_1_q));
  Multiplexer #(.width(32), .enable("false")) multiplexer_3 (
    .in0(32'h1), .in1(multiplexer_5_out), .out(multiplexer_3_out), .sel(d_ff_1_q));
  Multiplexer #(.width(32), .enable("false")) multiplexer_4 (
    .in0({32{1'b0}}), .in1(multiplexer_7_out), .out(multiplexer_4_out), .sel(d_ff_1_q));
  Register #(.width(32)) register_1 (.D(multiplexer_2_out), .Q(out_4), .clk(and_1_out), .clr(clear));  // open: en
  Register #(.width(32)) register_2 (
    .D(multiplexer_3_out), .Q(register_2_q), .clk(and_1_out), .clr(clear));  // open: en
  Register #(.width(32)) register_3 (
    .D(multiplexer_4_out), .Q(register_3_q), .clk(and_1_out), .clr(clear));  // open: en
  Register #(.width(32)) register_4 (
    .D(multiplexer_1_out), .Q(register_4_q), .clk(and_1_out), .clr(clear));  // open: en
  sqrX sqrx_1 (
    .a(register_3_q), .b(out_4), .c(register_4_q), .d(register_2_q), .a_prime(sqrx_1_a_prime),
    .b_prime(sqrx_1_b_prime), .c_prime(sqrx_1_c_prime), .d_prime(sqrx_1_d_prime));
  Multiplexer #(.width(32), .enable("false")) multiplexer_5 (
    .in0(sqrx_1_d_prime), .in1(sqrx_a_1_d_prime_prime), .out(multiplexer_5_out), .sel(\六位移位寄存器_1_out_15 ));
  sqrX_A sqrx_a_1 (
    .a(register_3_q), .b(out_4), .c(register_4_q), .d(register_2_q), .a_prime_prime(sqrx_a_1_a_prime_prime),
    .b_prime_prime(sqrx_a_1_b_prime_prime), .c_prime_prime(sqrx_a_1_c_prime_prime),
    .d_prime_prime(sqrx_a_1_d_prime_prime));
  Multiplexer #(.width(32), .enable("false")) multiplexer_6 (
    .in0(sqrx_1_c_prime), .in1(sqrx_a_1_c_prime_prime), .out(multiplexer_6_out), .sel(\六位移位寄存器_1_out_15 ));
  Multiplexer #(.width(32), .enable("false")) multiplexer_7 (
    .in0(sqrx_1_a_prime), .in1(sqrx_a_1_a_prime_prime), .out(multiplexer_7_out), .sel(\六位移位寄存器_1_out_15 ));
  Multiplexer #(.width(32), .enable("false")) multiplexer_8 (
    .in0(sqrx_1_b_prime), .in1(sqrx_a_1_b_prime_prime), .out(multiplexer_8_out), .sel(\六位移位寄存器_1_out_15 ));
endmodule

module \斐波那契_Fibonacci_数列计算器验证电路  (
  input  [5:0] in_1
);

  wire button_1_out, button_2_out;
  wire [3:0] \fibonacci数显示模块_1_out_2 , \fibonacci数显示模块_1_out_3 , \fibonacci数显示模块_1_out_4 ,
       \fibonacci数显示模块_1_out_5 , \fibonacci数显示模块_1_out_6 , \fibonacci数显示模块_1_out_7 ,
       \fibonacci数显示模块_1_out_8 , \fibonacci数显示模块_1_out_9 , \fibonacci数显示模块_1_out_10 ,
       \fibonacci数显示模块_1_out_11 ;
  wire [31:0] \斐波那契_fibonacci_数列计算器_1_out_4 ;

  Button button_1 (.out(button_1_out));
  Button button_2 (.out(button_2_out));
  \斐波那契_Fibonacci_数列计算器  \u_斐波那契_fibonacci_数列计算器_1  (
    .n(in_1), .clear(button_1_out), .clock(button_2_out), .out_4(\斐波那契_fibonacci_数列计算器_1_out_4 ));
  \Fibonacci数显示模块  \fibonacci数显示模块_1  (
    .in_1(\斐波那契_fibonacci_数列计算器_1_out_4 ), .out_2(\fibonacci数显示模块_1_out_2 ),
    .out_3(\fibonacci数显示模块_1_out_3 ), .out_4(\fibonacci数显示模块_1_out_4 ), .out_5(\fibonacci数显示模块_1_out_5 ),
    .out_6(\fibonacci数显示模块_1_out_6 ), .out_7(\fibonacci数显示模块_1_out_7 ), .out_8(\fibonacci数显示模块_1_out_8 ),
    .out_9(\fibonacci数显示模块_1_out_9 ), .out_10(\fibonacci数显示模块_1_out_10 ), .out_11(\fibonacci数显示模块_1_out_11 ));
  Hex_Digit_Display hex_digit_display_1 (.value(\fibonacci数显示模块_1_out_2 ));  // open: dp
  Hex_Digit_Display hex_digit_display_2 (.value(\fibonacci数显示模块_1_out_3 ));  // open: dp
  Hex_Digit_Display hex_digit_display_3 (.value(\fibonacci数显示模块_1_out_5 ));  // open: dp
  Hex_Digit_Display hex_digit_display_4 (.value(\fibonacci数显示模块_1_out_4 ));  // open: dp
  Hex_Digit_Display hex_digit_display_5 (.value(\fibonacci数显示模块_1_out_7 ));  // open: dp
  Hex_Digit_Display hex_digit_display_6 (.value(\fibonacci数显示模块_1_out_6 ));  // open: dp
  Hex_Digit_Display hex_digit_display_7 (.value(\fibonacci数显示模块_1_out_8 ));  // open: dp
  Hex_Digit_Display hex_digit_display_8 (.value(\fibonacci数显示模块_1_out_9 ));  // open: dp
  Hex_Digit_Display hex_digit_display_9 (.value(\fibonacci数显示模块_1_out_10 ));  // open: dp
  Hex_Digit_Display hex_digit_display_10 (.value(\fibonacci数显示模块_1_out_11 ));  // open: dp
endmodule

module c (
  input  in_1,
  input  in_2,
  input  in_3,
  input  in_4,
  output out_5,
  output out_6,
  output out_7,
  output out_8
);

  wire and_1_out, and_2_out, or_1_out;
  wire [3:0] adder_1_out;

  and and_1 (and_1_out, in_2, in_4);
  and and_2 (and_2_out, in_2, in_3);
  or or_1 (or_1_out, in_1, and_2_out, and_1_out);
  Adder #(.width(4)) adder_1 (.a({in_1, in_2, in_3, in_4}), .b(4'b0011), .out(adder_1_out), .cin(1'b0));  // open: cout
  Multiplexer #(.width(4), .enable("false")) multiplexer_1 (
    .in0({in_1, in_2, in_3, in_4}), .in1(adder_1_out), .out({out_5, out_6, out_7, out_8}), .sel(or_1_out));
endmodule

module \四位二进制可逆计数器  (
  input  D,
  input  C,
  input  B,
  input  A,
  input  nLD,
  input  CPu,
  input  CPd,
  input  CLR,
  output Qbb,
  output Qcc,
  output QD,
  output QC,
  output QB,
  output QA
);

  wire and_1_out, and_2_out, and_3_out, and_4_out, and_5_out, and_6_out, and_7_out, and_8_out, and_9_out,
       and_10_out, and_11_out, and_12_out, d_ff_1_qn, d_ff_2_qn, d_ff_3_qn, d_ff_4_qn, nor_1_out, nor_2_out,
       nor_3_out, nor_4_out, not_1_out, not_2_out, not_3_out, not_4_out, not_5_out, not_6_out, not_7_out,
       or_1_out, or_2_out, or_3_out, or_4_out, or_5_out, or_6_out, or_7_out, or_8_out;

  not not_1 (not_1_out, CPd);
  not not_2 (not_2_out, nLD);
  and and_1 (and_1_out, CPu, QC, QA, QB);
  nor nor_1 (nor_1_out, not_1_out, QC, QA, QB);
  and and_2 (and_2_out, CPu, QA, QB);
  nor nor_2 (nor_2_out, not_1_out, QA, QB);
  and and_3 (and_3_out, CPu, QA);
  nor nor_3 (nor_3_out, not_1_out, QA);
  and and_4 (and_4_out, not_2_out, D);
  or or_1 (or_1_out, and_1_out, nor_1_out);
  or or_2 (or_2_out, and_2_out, nor_2_out);
  or or_3 (or_3_out, and_3_out, nor_3_out);
  or or_4 (or_4_out, CPu, CPd);
  not not_3 (not_3_out, D);
  and and_5 (and_5_out, not_3_out, not_2_out);
  D_Flip_Flop #(.trigger("falling")) d_ff_1 (
    .clk(or_1_out), .D(d_ff_1_qn), .Q(QD), .Qn(d_ff_1_qn), .preset(and_4_out), .en(1'b1), .reset(or_5_out));
  or or_5 (or_5_out, CLR, and_5_out);
  and and_6 (and_6_out, not_2_out, C);
  D_Flip_Flop #(.trigger("falling")) d_ff_2 (
    .clk(or_2_out), .D(d_ff_2_qn), .Q(QC), .Qn(d_ff_2_qn), .preset(and_6_out), .en(1'b1), .reset(or_6_out));
  or or_6 (or_6_out, CLR, and_8_out);
  not not_4 (not_4_out, C);
  and and_7 (and_7_out, not_2_out, B);
  and and_8 (and_8_out, not_4_out, not_2_out);
  not not_5 (not_5_out, B);
  and and_9 (and_9_out, not_5_out, not_2_out);
  D_Flip_Flop #(.trigger("falling")) d_ff_3 (
    .clk(or_3_out), .D(d_ff_3_qn), .Q(QB), .Qn(d_ff_3_qn), .preset(and_7_out), .en(1'b1), .reset(or_7_out));
  or or_7 (or_7_out, CLR, and_9_out);
  and and_10 (and_10_out, not_2_out, A);
  or or_8 (or_8_out, CLR, and_11_out);
  not not_6 (not_6_out, A);
  and and_11 (and_11_out, not_6_out, not_2_out);
  D_Flip_Flop #(.trigger("falling")) d_ff_4 (
    .clk(or_4_out), .D(d_ff_4_qn), .Q(QA), .Qn(d_ff_4_qn), .preset(and_10_out), .en(1'b1), .reset(or_8_out));
  nor nor_4 (nor_4_out, QD, QC, QB, QA, not_7_out);
  and and_12 (and_12_out, QD, QC, QB, QA, CPu);
  not not_7 (not_7_out, CPd);
  and and_13 (Qbb, nLD, nor_4_out);
  and and_14 (Qcc, nLD, and_12_out);
endmodule

module \八位二进制计数器  (
  input  [7:0] in_1,
  input  CPu,
  input  en,
  input  CLR,
  input  nLD,
  output Carry,
  output [7:0] out_7
);

  wire and_1_out, \四位二进制可逆计数器_1_qbb , \四位二进制可逆计数器_1_qcc ;

  and and_1 (and_1_out, CPu, en);
  \四位二进制可逆计数器  \u_四位二进制可逆计数器_1  (
    .Qbb(\四位二进制可逆计数器_1_qbb ), .D(in_1[3]), .C(in_1[2]), .B(in_1[1]), .A(in_1[0]), .Qcc(\四位二进制可逆计数器_1_qcc ),
    .nLD(nLD), .QD(out_7[3]), .QC(out_7[2]), .QB(out_7[1]), .QA(out_7[0]), .CPu(and_1_out), .CPd(1'b0),
    .CLR(CLR));
  \四位二进制可逆计数器  \u_四位二进制可逆计数器_2  (
    .D(in_1[7]), .C(in_1[6]), .B(in_1[5]), .A(in_1[4]), .Qcc(Carry), .nLD(nLD), .QD(out_7[7]), .QC(out_7[6]),
    .QB(out_7[5]), .QA(out_7[4]), .CPu(\四位二进制可逆计数器_1_qcc ), .CPd(\四位二进制可逆计数器_1_qbb ), .CLR(CLR));  // open: Qbb
endmodule

module \六位移位寄存器  (
  input  clk,
  input  clr,
  input  LD,
  input  in_4,
  input  in_5,
  input  in_6,
  input  in_7,
  input  in_8,
  input  in_9,
  output out_10,
  output out_11,
  output out_12,
  output out_13,
  output out_14,
  output out_15,
  output out_16
);

  wire and_1_out, and_2_out, and_3_out, and_4_out, and_5_out, and_6_out, and_7_out, and_8_out, and_9_out,
       and_10_out, and_11_out, and_12_out, not_1_out, not_2_out, not_3_out, not_4_out, not_5_out, not_6_out,
       or_1_out, or_2_out, or_3_out, or_4_out, or_5_out, or_6_out, or_7_out;

  D_Flip_Flop d_ff_1 (.clk(clk), .D(1'b0), .Q(out_10), .preset(and_2_out), .en(1'b1), .reset(or_1_out));  // open: Qn
  or or_1 (or_1_out, clr, and_1_out);
  and and_1 (and_1_out, LD, not_2_out);
  and and_2 (and_2_out, LD, in_4);
  D_Flip_Flop d_ff_2 (.clk(clk), .D(out_10), .Q(out_11), .preset(and_4_out), .en(1'b1), .reset(or_2_out));  // open: Qn
  or or_2 (or_2_out, clr, and_3_out);
  and and_3 (and_3_out, LD, not_1_out);
  and and_4 (and_4_out, LD, in_5);
  not not_1 (not_1_out, in_5);
  not not_2 (not_2_out, in_4);
  D_Flip_Flop d_ff_3 (.clk(clk), .D(out_11), .Q(out_12), .preset(and_7_out), .en(1'b1), .reset(or_3_out));  // open: Qn
  or or_3 (or_3_out, clr, and_6_out);
  and and_5 (and_5_out, LD, in_7);
  and and_6 (and_6_out, LD, not_3_out);
  and and_7 (and_7_out, LD, in_6);
  not not_3 (not_3_out, in_6);
  D_Flip_Flop d_ff_4 (.clk(clk), .D(out_12), .Q(out_13), .preset(and_5_out), .en(1'b1), .reset(or_4_out));  // open: Qn
  D_Flip_Flop d_ff_5 (.clk(clk), .D(out_13), .Q(out_14), .preset(and_8_out), .en(1'b1), .reset(or_5_out));  // open: Qn
  or or_4 (or_4_out, clr, and_10_out);
  or or_5 (or_5_out, clr, and_9_out);
  and and_8 (and_8_out, LD, in_8);
  and and_9 (and_9_out, LD, not_6_out);
  and and_10 (and_10_out, LD, not_4_out);
  not not_4 (not_4_out, in_7);
  D_Flip_Flop d_ff_6 (.clk(clk), .D(out_14), .Q(out_15), .preset(and_11_out), .en(1'b1), .reset(or_6_out));  // open: Qn
  or or_6 (or_6_out, clr, and_12_out);
  and and_11 (and_11_out, LD, in_9);
  and and_12 (and_12_out, LD, not_5_out);
  not not_5 (not_5_out, in_9);
  not not_6 (not_6_out, in_8);
  D_Flip_Flop d_ff_7 (.clk(clk), .D(out_15), .Q(out_16), .en(1'b1), .reset(or_7_out));  // open: Qn, preset
  or or_7 (or_7_out, clr, LD);
endmodule
